// Logisim project 8bit_computer.circ as structural Verilog: 11 circuits, main circuit main
module main (
  input  in_1,
  input  in_2,
  input  in_3,
  input  in_4,
  input  in_5,
  input  in_6,
  output [7:0] out_7
);

  wire AI, alu_1_cy, AO, BI, CE, clock_1_out, clock_circuit_1_clk_2, CO, control_unit_1_out_3, EO, HLT, II,
       IO, J, MI, OI, RI, RO, SU;
  wire [3:0] display_hex_1_hex1, display_hex_1_hex2, display_hex_1_hex3, display_hex_1_hex4,
       mem_addr_reg_1_out, mem_addr_reg_1_value, program_counter_1_value;
  wire [7:0] alu_1_value, instruction_reg_1_out, n8_bit_register_1_value, n8_bit_register_2_value, rom_1_data;

  ROM #(.addrWidth(4)) rom_1 (.addr(mem_addr_reg_1_out), .data(rom_1_data));
  Clock clock_1 (.out(clock_1_out));
  Control_Unit control_unit_1 (
    .CLK(clock_circuit_1_clk_2), .Addr(out_7), .out_3(control_unit_1_out_3), .J(J), .CO(CO), .CE(CE),
    .OI(OI), .BI(BI), .SU(SU), .EO(EO), .AO(AO), .AI(AI), .II(II), .IO(IO), .RO(RO), .RI(RI), .MI(MI),
    .HLT(HLT));
  Clock_circuit clock_circuit_1 (.clk(clock_1_out), .HLT(HLT), .CLK_2(clock_circuit_1_clk_2));
  DotMatrix #(.matrixcols(4), .matrixrows(1)) dotmatrix_1 (
    .col0(mem_addr_reg_1_value[3]), .col1(mem_addr_reg_1_value[2]), .col2(mem_addr_reg_1_value[1]),
    .col3(mem_addr_reg_1_value[0]));
  Mem_Addr_Reg mem_addr_reg_1 (
    .IN(instruction_reg_1_out), .CLK(clock_circuit_1_clk_2), .LOAD(MI), .CLR(in_2),
    .value(mem_addr_reg_1_value), .OUT(mem_addr_reg_1_out));
  DotMatrix #(.matrixcols(8), .matrixrows(1)) dotmatrix_2 (
    .col0(rom_1_data[7]), .col1(rom_1_data[6]), .col2(rom_1_data[5]), .col3(rom_1_data[4]),
    .col4(rom_1_data[3]), .col5(rom_1_data[2]), .col6(rom_1_data[1]), .col7(rom_1_data[0]));
  DotMatrix #(.matrixcols(8), .matrixrows(1)) dotmatrix_3 (
    .col0(out_7[7]), .col1(out_7[6]), .col2(out_7[5]), .col3(out_7[4]), .col4(out_7[3]), .col5(out_7[2]),
    .col6(out_7[1]), .col7(out_7[0]));
  Instruction_Reg instruction_reg_1 (
    .IN(instruction_reg_1_out), .CLK(clock_circuit_1_clk_2), .LOAD(II), .CLR(in_4), .OE(IO), .value(out_7),
    .OUT(instruction_reg_1_out));
  assign instruction_reg_1_out = RO ? rom_1_data : 8'bz;  // Controlled_Buffer controlled_buffer_1
  DotMatrix #(.matrixcols(8), .matrixrows(1)) dotmatrix_4 (
    .col0(instruction_reg_1_out[7]), .col1(instruction_reg_1_out[6]), .col2(instruction_reg_1_out[5]),
    .col3(instruction_reg_1_out[4]), .col4(instruction_reg_1_out[3]), .col5(instruction_reg_1_out[2]),
    .col6(instruction_reg_1_out[1]), .col7(instruction_reg_1_out[0]));
  Pull_Resistor pull_resistor_1 (.node(instruction_reg_1_out));
  Hex_Digit_Display hex_digit_display_1 (.value(display_hex_1_hex4));  // open: dp
  Display_hex display_hex_1 (
    .IN(instruction_reg_1_out), .CLK(clock_circuit_1_clk_2), .Sign(in_1), .ENABLE(OI),
    .hex4(display_hex_1_hex4), .hex3(display_hex_1_hex3), .hex2(display_hex_1_hex2), .hex1(display_hex_1_hex1));
  DotMatrix #(.matrixcols(4), .matrixrows(1)) dotmatrix_5 (
    .col0(program_counter_1_value[3]), .col1(program_counter_1_value[2]), .col2(program_counter_1_value[1]),
    .col3(program_counter_1_value[0]));
  Program_Counter program_counter_1 (
    .IN(instruction_reg_1_out), .CLK(clock_circuit_1_clk_2), .J(J), .CE(CE), .CO(CO),
    .value(program_counter_1_value), .OUT(instruction_reg_1_out));
  DotMatrix #(.matrixcols(8), .matrixrows(1)) dotmatrix_6 (
    .col0(n8_bit_register_1_value[7]), .col1(n8_bit_register_1_value[6]), .col2(n8_bit_register_1_value[5]),
    .col3(n8_bit_register_1_value[4]), .col4(n8_bit_register_1_value[3]), .col5(n8_bit_register_1_value[2]),
    .col6(n8_bit_register_1_value[1]), .col7(n8_bit_register_1_value[0]));
  _8_bit_Register u_8_bit_register_1 (
    .IN(instruction_reg_1_out), .CLK(clock_circuit_1_clk_2), .LOAD(AI), .CLR(in_3), .OE(AO),
    .value(n8_bit_register_1_value), .OUT(instruction_reg_1_out));
  DotMatrix #(.matrixcols(8), .matrixrows(1)) dotmatrix_7 (
    .col0(alu_1_value[7]), .col1(alu_1_value[6]), .col2(alu_1_value[5]), .col3(alu_1_value[4]),
    .col4(alu_1_value[3]), .col5(alu_1_value[2]), .col6(alu_1_value[1]), .col7(alu_1_value[0]));
  ALU alu_1 (
    .value(alu_1_value), .Result(instruction_reg_1_out), .CY(alu_1_cy), .SU(SU), .Select(1'b1), .EO(EO),
    .B(n8_bit_register_2_value), .A(n8_bit_register_1_value));
  DotMatrix #(.matrixcols(8), .matrixrows(1)) dotmatrix_8 (
    .col0(n8_bit_register_2_value[7]), .col1(n8_bit_register_2_value[6]), .col2(n8_bit_register_2_value[5]),
    .col3(n8_bit_register_2_value[4]), .col4(n8_bit_register_2_value[3]), .col5(n8_bit_register_2_value[2]),
    .col6(n8_bit_register_2_value[1]), .col7(n8_bit_register_2_value[0]));
  _8_bit_Register u_8_bit_register_2 (
    .IN(instruction_reg_1_out), .CLK(clock_circuit_1_clk_2), .LOAD(BI), .CLR(in_5), .OE(in_6),
    .value(n8_bit_register_2_value), .OUT(instruction_reg_1_out));
  Hex_Digit_Display hex_digit_display_2 (.value(display_hex_1_hex3));  // open: dp
  Hex_Digit_Display hex_digit_display_3 (.value(display_hex_1_hex2));  // open: dp
  LED led_1 (.in(alu_1_cy));
  Hex_Digit_Display hex_digit_display_4 (.value(display_hex_1_hex1));  // open: dp

  // Notes on the sheet:
  //   LDA  = 0001
  //   ADD = 0010
  //   SUB = 0011
  //   OUT = 1110
  //   JMP = 1111
  //   CODE : 
  //   	   LDA 14
  //   	  ADD 15
  //     OUT
  //    SUB
  //   	 JMP  &2
  //   contents of rom_1 (hex, n*v repeats v):
  //   1e 2f e0 30 f2 9*0 1
endmodule

module Clock_circuit (
  input  clk,
  input  HLT,
  output CLK_2
);

  wire not_1_out;

  not not_1 (not_1_out, HLT);
  and and_1 (CLK_2, clk, not_1_out);
endmodule

module _8_bit_Register (
  input  [7:0] IN,
  input  CLK,
  input  LOAD,
  input  CLR,
  input  OE,
  output [7:0] value,
  output [7:0] OUT
);

  wire [7:0] controlled_buffer_1_out;

  assign controlled_buffer_1_out = LOAD ? IN : 8'bz;  // Controlled_Buffer controlled_buffer_1
  Register register_1 (.D(controlled_buffer_1_out), .Q(value), .clk(CLK), .clr(CLR));  // open: en
  assign OUT = OE ? value : 8'bz;  // Controlled_Buffer controlled_buffer_2
endmodule

module Mem_Addr_Reg (
  input  [7:0] IN,
  input  CLK,
  input  LOAD,
  input  CLR,
  output [3:0] value,
  output [3:0] OUT
);

  wire [3:0] controlled_buffer_1_out;

  assign controlled_buffer_1_out = LOAD ? IN[3:0] : 4'bz;  // Controlled_Buffer controlled_buffer_1
  Register #(.width(4)) register_1 (.D(controlled_buffer_1_out), .Q(OUT), .clk(CLK), .clr(CLR));  // open: en

  assign value = OUT;
endmodule

module Instruction_Reg (
  input  [7:0] IN,
  input  CLK,
  input  LOAD,
  input  CLR,
  input  OE,
  output [7:0] value,
  output [7:0] OUT
);

  wire [7:0] controlled_buffer_1_out;

  assign controlled_buffer_1_out = LOAD ? IN : 8'bz;  // Controlled_Buffer controlled_buffer_1
  Register register_1 (.D(controlled_buffer_1_out), .Q(value), .clk(CLK), .clr(CLR));  // open: en
  assign OUT = OE ? value : 8'bz;  // Controlled_Buffer controlled_buffer_2
endmodule

module ALU (
  input  [7:0] A,
  input  SU,
  input  Select,
  input  EO,
  input  [7:0] B,
  output [7:0] value,
  output [7:0] Result,
  output CY
);

  wire [7:0] controlled_buffer_1_out, controlled_buffer_2_out, controlled_buffer_3_out, xor_1_out;

  assign controlled_buffer_1_out = SU ? {8{1'b1}} : 8'bz;  // Controlled_Buffer controlled_buffer_1
  Pull_Resistor pull_resistor_1 (.node(controlled_buffer_1_out));
  assign controlled_buffer_2_out = Select ? A : 8'bz;  // Controlled_Buffer controlled_buffer_2
  assign controlled_buffer_3_out = Select ? B : 8'bz;  // Controlled_Buffer controlled_buffer_3
  Adder adder_1 (.a(controlled_buffer_2_out), .b(xor_1_out), .out(value), .cin(SU), .cout(CY));
  assign xor_1_out = controlled_buffer_1_out ^ controlled_buffer_3_out;  // XOR_Gate xor_1, 8 bits wide
  assign Result = EO ? value : 8'bz;  // Controlled_Buffer controlled_buffer_4
endmodule

module RAM_16B (
  input  CLK,
  input  [3:0] Addr,
  input  [3:0] Addr__p,
  input  WE,
  input  WE__p,
  input  [7:0] Data,
  input  [7:0] Data__p,
  input  Mode,
  input  RO,
  output [7:0] value,
  output [7:0] OUT
);

  wire multiplexer_2_out;
  wire [3:0] multiplexer_1_out;
  wire [7:0] multiplexer_3_out;

  Multiplexer #(.enable("false"), .width(4)) multiplexer_1 (
    .in0(Addr), .in1(Addr__p), .out(multiplexer_1_out), .sel(Mode));
  RAM #(.addrWidth(4)) ram_1 (
    .addr(multiplexer_1_out), .we(multiplexer_2_out), .clk(CLK), .din(multiplexer_3_out), .dout(value));
  Multiplexer #(.enable("false")) multiplexer_2 (.in0(WE), .in1(WE__p), .out(multiplexer_2_out), .sel(Mode));
  Multiplexer #(.enable("false"), .width(8)) multiplexer_3 (
    .in0(Data), .in1(Data__p), .out(multiplexer_3_out), .sel(Mode));
  assign OUT = RO ? value : 8'bz;  // Controlled_Buffer controlled_buffer_1
endmodule

module Program_Counter (
  input  [7:0] IN,
  input  CLK,
  input  J,
  input  CE,
  input  CO,
  output [3:0] value,
  output [7:0] OUT
);

  Counter #(.max('hf), .width(4)) counter_1 (
    .load(J), .D(IN[3:0]), .count(CE), .Q(value), .clk(CLK));  // open: carry, clr
  assign OUT[3:0] = CO ? value : 4'bz;  // Controlled_Buffer controlled_buffer_1
endmodule

module Display_7seg (
  input  [7:0] IN,
  input  CLK,
  input  Sign,
  input  ENABLE,
  output [7:0] _7seg4,
  output [7:0] _7seg3,
  output [7:0] _7seg2,
  output [7:0] _7seg1
);

  wire and_1_out, demultiplexer_1_out0, demultiplexer_1_out1, demultiplexer_1_out2, demultiplexer_1_out3;
  wire [7:0] register_1_q, rom_1_data;
  wire [9:8] counter_1_q;

  Register register_1 (.D(IN), .Q(register_1_q), .clk(and_1_out));  // open: en, clr
  and and_1 (and_1_out, ENABLE, CLK);
  Counter #(.max('h3), .width(2)) counter_1 (
    .count(1'b1), .Q(counter_1_q), .up(1'b0), .clk(CLK));  // open: load, D, carry, clr
  ROM #(.addrWidth(11)) rom_1 (.addr({Sign, counter_1_q, register_1_q}), .data(rom_1_data));
  Demultiplexer #(.enable("false"), .select(2)) demultiplexer_1 (
    .out0(demultiplexer_1_out0), .out1(demultiplexer_1_out1), .out2(demultiplexer_1_out2),
    .out3(demultiplexer_1_out3), .in(1'b1), .sel(counter_1_q));
  Pull_Resistor pull_resistor_1 (.node(demultiplexer_1_out0));
  Pull_Resistor pull_resistor_2 (.node(demultiplexer_1_out1));
  Pull_Resistor pull_resistor_3 (.node(demultiplexer_1_out2));
  Pull_Resistor pull_resistor_4 (.node(demultiplexer_1_out3));
  Register register_2 (.D(rom_1_data), .en(demultiplexer_1_out0), .Q(_7seg1), .clk(CLK));  // open: clr
  Register register_3 (.D(rom_1_data), .en(demultiplexer_1_out1), .Q(_7seg2), .clk(CLK));  // open: clr
  Register register_4 (.D(rom_1_data), .en(demultiplexer_1_out2), .Q(_7seg3), .clk(CLK));  // open: clr
  Register register_5 (.D(rom_1_data), .en(demultiplexer_1_out3), .Q(_7seg4), .clk(CLK));  // open: clr

  // Notes on the sheet:
  //   contents of rom_1 (hex, n*v repeats v):
  //   3f 6 5b 4f 66 6d 7d 7 7f 6f 3f 6 5b 4f 66 6d 7d 7 7f 6f 3f 6 5b 4f 66 6d 7d 7 7f 6f 3f 6 5b 4f 66 6d
  //   7d 7 7f 6f 3f 6 5b 4f 66 6d 7d 7 7f 6f 3f 6 5b 4f 66 6d 7d 7 7f 6f 3f 6 5b 4f 66 6d 7d 7 7f 6f 3f 6
  //   5b 4f 66 6d 7d 7 7f 6f 3f 6 5b 4f 66 6d 7d 7 7f 6f 3f 6 5b 4f 66 6d 7d 7 7f 6f 3f 6 5b 4f 66 6d 7d 7
  //   7f 6f 3f 6 5b 4f 66 6d 7d 7 7f 6f 3f 6 5b 4f 66 6d 7d 7 7f 6f 3f 6 5b 4f 66 6d 7d 7 7f 6f 3f 6 5b 4f
  //   66 6d 7d 7 7f 6f 3f 6 5b 4f 66 6d 7d 7 7f 6f 3f 6 5b 4f 66 6d 7d 7 7f 6f 3f 6 5b 4f 66 6d 7d 7 7f 6f
  //   3f 6 5b 4f 66 6d 7d 7 7f 6f 3f 6 5b 4f 66 6d 7d 7 7f 6f 3f 6 5b 4f 66 6d 7d 7 7f 6f 3f 6 5b 4f 66 6d
  //   7d 7 7f 6f 3f 6 5b 4f 66 6d 7d 7 7f 6f 3f 6 5b 4f 66 6d 7d 7 7f 6f 3f 6 5b 4f 66 6d 7d 7 7f 6f 3f 6
  //   5b 4f 66 6d 10*3f 10*6 10*5b 10*4f 10*66 10*6d 10*7d 10*7 10*7f 10*6f 10*3f 10*6 10*5b 10*4f 10*66
  //   10*6d 10*7d 10*7 10*7f 10*6f 10*3f 10*6 10*5b 10*4f 10*66 6*6d 100*3f 100*6 56*5b 256*0 3f 6 5b 4f
  //   66 6d 7d 7 7f 6f 3f 6 5b 4f 66 6d 7d 7 7f 6f 3f 6 5b 4f 66 6d 7d 7 7f 6f 3f 6 5b 4f 66 6d 7d 7 7f 6f
  //   3f 6 5b 4f 66 6d 7d 7 7f 6f 3f 6 5b 4f 66 6d 7d 7 7f 6f 3f 6 5b 4f 66 6d 7d 7 7f 6f 3f 6 5b 4f 66 6d
  //   7d 7 7f 6f 3f 6 5b 4f 66 6d 7d 7 7f 6f 3f 6 5b 4f 66 6d 7d 7 7f 6f 3f 6 5b 4f 66 6d 7d 7 7f 6f 3f 6
  //   5b 4f 66 6d 7d 7 7f 6f 3f 6 5b 4f 66 6d 7d 7 7f 7 7d 6d 66 4f 5b 6 3f 6f 7f 7 7d 6d 66 4f 5b 6 3f 6f
  //   7f 7 7d 6d 66 4f 5b 6 3f 6f 7f 7 7d 6d 66 4f 5b 6 3f 6f 7f 7 7d 6d 66 4f 5b 6 3f 6f 7f 7 7d 6d 66 4f
  //   5b 6 3f 6f 7f 7 7d 6d 66 4f 5b 6 3f 6f 7f 7 7d 6d 66 4f 5b 6 3f 6f 7f 7 7d 6d 66 4f 5b 6 3f 6f 7f 7
  //   7d 6d 66 4f 5b 6 3f 6f 7f 7 7d 6d 66 4f 5b 6 3f 6f 7f 7 7d 6d 66 4f 5b 6 3f 6f 7f 7 7d 6d 66 4f 5b 6
  //   10*3f 10*6 10*5b 10*4f 10*66 10*6d 10*7d 10*7 10*7f 10*6f 10*3f 10*6 17*5b 10*6 10*3f 10*6f 10*7f
  //   10*7 10*7d 10*6d 10*66 10*4f 10*5b 10*6 109*3f 57*6 99*3f 128*0 128*40
endmodule

module Control_Unit (
  input  CLK,
  input  [7:0] Addr,
  output out_3,
  output J,
  output CO,
  output CE,
  output OI,
  output BI,
  output SU,
  output EO,
  output AO,
  output AI,
  output II,
  output IO,
  output RO,
  output RI,
  output MI,
  output HLT
);

  wire decoder_1_out6;
  wire [2:0] counter_1_q;

  Decoder #(.select(3)) decoder_1 (
    .out6(decoder_1_out6), .sel(counter_1_q));  // open: out0, out1, out2, out3, out4, out5, out7, en
  Counter #(.max('h7), .width(3)) counter_1 (
    .count(1'b1), .Q(counter_1_q), .clk(CLK), .clr(decoder_1_out6));  // open: load, D, carry
  ROM #(.addrWidth(7), .dataWidth(16)) rom_1 (
    .addr({Addr[7:4], counter_1_q}),
    .data({HLT, MI, RI, RO, IO, II, AI, AO, EO, SU, BI, OI, CE, CO, J, out_3}));

  // Notes on the sheet:
  //   contents of rom_1 (hex, n*v repeats v):
  //   4004 1408 6*0 4004 1408 4800 1200 4*0 4004 1408 4800 1020 280 0 0 0 4004 1408 e0 280 4*0 4004 1408
  //   6*0 4004 1408 6*0 4004 1408 6*0 4004 1408 6*0 4004 1408 6*0 4004 1408 6*0 4004 1408 6*0 4004 1408
  //   6*0 4004 1408 6*0 4004 1408 6*0 4004 1408 110 5*0 4004 1408 802
endmodule

module Display_hex (
  input  [7:0] IN,
  input  CLK,
  input  Sign,
  input  ENABLE,
  output [3:0] hex4,
  output [3:0] hex3,
  output [3:0] hex2,
  output [3:0] hex1
);

  wire comparator_1_gt, nand_1_out;
  wire [7:0] register_1_q;

  Register register_1 (.D(IN), .en(ENABLE), .Q(register_1_q), .clk(CLK));  // open: clr
  ROM #(.addrWidth(9), .dataWidth(12)) rom_1 (.addr({Sign, register_1_q}), .data({hex3, hex2, hex1}));
  Comparator #(.mode("unsigned")) comparator_1 (.a(register_1_q), .b(8'h7f), .gt(comparator_1_gt));  // open: eq, lt
  nand nand_1 (nand_1_out, Sign, comparator_1_gt);
  assign hex4 = nand_1_out ? 4'b0000 : 4'bz;  // Controlled_Buffer controlled_buffer_1

  // Notes on the sheet:
  //   contents of rom_1 (hex, n*v repeats v):
  //   0 1 2 3 4 5 6 7 8 9 10 11 12 13 14 15 16 17 18 19 20 21 22 23 24 25 26 27 28 29 30 31 32 33 34 35 36
  //   37 38 39 40 41 42 43 44 45 46 47 48 49 50 51 52 53 54 55 56 57 58 59 60 61 62 63 64 65 66 67 68 69
  //   70 71 72 73 74 75 76 77 78 79 80 81 82 83 84 85 86 87 88 89 90 91 92 93 94 95 96 97 98 99 100 101
  //   102 103 104 105 106 107 108 109 110 111 112 113 114 115 116 117 118 119 120 121 122 123 124 125 126
  //   127 128 129 130 131 132 133 134 135 136 137 138 139 140 141 142 143 144 145 146 147 148 149 150 151
  //   152 153 154 155 156 157 158 159 160 161 162 163 164 165 166 167 168 169 170 171 172 173 174 175 176
  //   177 178 179 180 181 182 183 184 185 186 187 188 189 190 191 192 193 194 195 196 197 198 199 200 201
  //   202 203 204 205 206 207 208 209 210 211 212 213 214 215 216 217 218 219 220 221 222 223 224 225 226
  //   227 228 229 230 231 232 233 234 235 236 237 238 239 240 241 242 243 244 245 246 247 248 249 250 251
  //   252 253 254 255 0 1 2 3 4 5 6 7 8 9 10 11 12 13 14 15 16 17 18 19 20 21 22 23 24 25 26 27 28 29 30
  //   31 32 33 34 35 36 37 38 39 40 41 42 43 44 45 46 47 48 49 50 51 52 53 54 55 56 57 58 59 60 61 62 63
  //   64 65 66 67 68 69 70 71 72 73 74 75 76 77 78 79 80 81 82 83 84 85 86 87 88 89 90 91 92 93 94 95 96
  //   97 98 99 100 101 102 103 104 105 106 107 108 109 110 111 112 113 114 115 116 117 118 119 120 121 122
  //   123 124 125 126 127 128 127 126 125 124 123 122 121 120 119 118 117 116 115 114 113 112 111 110 109
  //   108 107 106 105 104 103 102 101 100 99 98 97 96 95 94 93 92 91 90 89 88 87 86 85 84 83 82 81 80 79
  //   78 77 76 75 74 73 72 71 70 69 68 67 66 65 64 63 62 61 60 59 58 57 56 55 54 53 52 51 50 49 48 47 46
  //   45 44 43 42 41 40 39 38 37 36 35 34 33 32 31 30 29 28 27 26 25 24 23 22 21 20 19 18 17 16 15 14 13
  //   12 11 10 9 8 7 6 5 4 3 2 1
endmodule
