// Logisim project 8-bit_ALU.circ as structural Verilog
module FA (
  input  Cin,
  input  A,
  input  B,
  output Cout,
  output SUM,
  output AND,
  output XOR,
  output OR
);

  wire ha_2_c;

  or or_1 (Cout, AND, ha_2_c);
  HA ha_1 (.C(AND), .SUM(XOR), .A(A), .B(B));
  HA ha_2 (.C(ha_2_c), .SUM(SUM), .A(Cin), .B(XOR));
  or or_2 (OR, A, B);
endmodule

module HA (
  input  A,
  input  B,
  output C,
  output SUM
);

  and and_1 (C, A, B);
  xor xor_1 (SUM, A, B);
endmodule

module FA_2 (
  input  Ci,
  input  A,
  input  B,
  output Co,
  output S
);

  wire ha_1_c, ha_1_sum, ha_2_c;

  or or_1 (Co, ha_1_c, ha_2_c);
  HA ha_1 (.C(ha_1_c), .SUM(ha_1_sum), .A(A), .B(B));
  HA ha_2 (.C(ha_2_c), .SUM(S), .A(Ci), .B(ha_1_sum));
endmodule

module _8_bit_Adder (
  input  [7:0] B,
  input  [7:0] A,
  input  B_inv,
  input  A_inv,
  input  Cin,
  output C,
  output N,
  output V,
  output [7:0] AND,
  output [7:0] XOR,
  output [7:0] OR,
  output Z,
  output [7:0] SUM
);

  wire fa_2_cout, fa_3_cout, fa_4_cout, fa_5_cout, fa_6_cout, fa_7_cout, fa_8_cout, xor_2_out, xor_3_out,
       xor_4_out, xor_5_out, xor_6_out, xor_7_out, xor_8_out, xor_9_out, xor_10_out, xor_11_out, xor_12_out,
       xor_13_out, xor_14_out, xor_15_out, xor_16_out, xor_17_out;

  xor xor_1 (V, fa_2_cout, fa_3_cout);
  nor nor_1 (Z, N, SUM[6], SUM[5], SUM[4], SUM[3], SUM[2], SUM[1], SUM[0]);
  xor xor_2 (xor_2_out, A[7], A_inv);
  FA fa_1 (.Cout(C), .SUM(N), .AND(AND[7]), .XOR(XOR[7]), .OR(OR[7]), .Cin(fa_2_cout), .A(xor_2_out), .B(xor_3_out));
  xor xor_3 (xor_3_out, B[7], B_inv);
  xor xor_4 (xor_4_out, A[6], A_inv);
  FA fa_2 (
    .Cout(fa_2_cout), .SUM(SUM[6]), .AND(AND[6]), .XOR(XOR[6]), .OR(OR[6]), .Cin(fa_3_cout), .A(xor_4_out),
    .B(xor_5_out));
  xor xor_5 (xor_5_out, B[6], B_inv);
  FA fa_3 (
    .Cout(fa_3_cout), .SUM(SUM[5]), .AND(AND[5]), .XOR(XOR[5]), .OR(OR[5]), .Cin(fa_4_cout), .A(xor_7_out),
    .B(xor_6_out));
  xor xor_6 (xor_6_out, B[5], B_inv);
  xor xor_7 (xor_7_out, A[5], A_inv);
  xor xor_8 (xor_8_out, A[4], A_inv);
  FA fa_4 (
    .Cout(fa_4_cout), .SUM(SUM[4]), .AND(AND[4]), .XOR(XOR[4]), .OR(OR[4]), .Cin(fa_5_cout), .A(xor_8_out),
    .B(xor_9_out));
  xor xor_9 (xor_9_out, B[4], B_inv);
  xor xor_10 (xor_10_out, B[3], B_inv);
  xor xor_11 (xor_11_out, A[3], A_inv);
  FA fa_5 (
    .Cout(fa_5_cout), .SUM(SUM[3]), .AND(AND[3]), .XOR(XOR[3]), .OR(OR[3]), .Cin(fa_6_cout), .A(xor_11_out),
    .B(xor_10_out));
  FA fa_6 (
    .Cout(fa_6_cout), .SUM(SUM[2]), .AND(AND[2]), .XOR(XOR[2]), .OR(OR[2]), .Cin(fa_7_cout), .A(xor_13_out),
    .B(xor_12_out));
  xor xor_12 (xor_12_out, B[2], B_inv);
  xor xor_13 (xor_13_out, A[2], A_inv);
  xor xor_14 (xor_14_out, A[1], A_inv);
  FA fa_7 (
    .Cout(fa_7_cout), .SUM(SUM[1]), .AND(AND[1]), .XOR(XOR[1]), .OR(OR[1]), .Cin(fa_8_cout), .A(xor_14_out),
    .B(xor_15_out));
  xor xor_15 (xor_15_out, B[1], B_inv);
  FA fa_8 (
    .Cout(fa_8_cout), .SUM(SUM[0]), .AND(AND[0]), .XOR(XOR[0]), .OR(OR[0]), .Cin(Cin), .A(xor_17_out),
    .B(xor_16_out));
  xor xor_16 (xor_16_out, B[0], B_inv);
  xor xor_17 (xor_17_out, A[0], A_inv);

  assign SUM[7] = N;
endmodule

module _8_bit_Multiplier (
  input  [7:0] A,
  input  [7:0] B,
  output [15:0] P
);

  wire and_1_out, and_2_out, and_3_out, and_4_out, and_5_out, and_6_out, and_7_out, and_8_out, and_9_out,
       and_10_out, and_11_out, and_12_out, and_13_out, and_14_out, and_15_out, and_16_out, and_17_out,
       and_18_out, and_19_out, and_20_out, and_21_out, and_22_out, and_23_out, and_24_out, and_25_out,
       and_26_out, and_27_out, and_28_out, and_29_out, and_30_out, and_31_out, and_32_out, and_33_out,
       and_34_out, and_35_out, and_36_out, and_37_out, and_38_out, and_39_out, and_40_out, and_41_out,
       and_42_out, and_43_out, and_44_out, and_45_out, and_46_out, and_47_out, and_48_out, and_49_out,
       and_50_out, and_51_out, and_52_out, and_53_out, and_54_out, and_55_out, and_56_out, and_57_out,
       and_58_out, and_59_out, and_60_out, and_61_out, and_62_out, and_63_out, fa_2_co, fa_3_co, fa_3_s,
       fa_4_co, fa_5_co, fa_5_s, fa_6_co, fa_6_s, fa_7_co, fa_7_s, fa_8_co, fa_9_co, fa_9_s, fa_10_co,
       fa_11_co, fa_11_s, fa_12_co, fa_12_s, fa_13_co, fa_13_s, fa_14_co, fa_14_s, fa_15_co, fa_15_s,
       fa_16_co, fa_17_co, fa_17_s, fa_18_co, fa_18_s, fa_19_co, fa_19_s, fa_20_co, fa_21_co, fa_21_s,
       fa_22_co, fa_22_s, fa_23_co, fa_23_s, fa_24_co, fa_24_s, fa_25_co, fa_25_s, fa_26_co, fa_26_s,
       fa_27_co, fa_27_s, fa_28_co, fa_28_s, fa_29_co, fa_29_s, fa_30_co, fa_30_s, fa_31_co, fa_31_s,
       fa_32_co, fa_32_s, fa_33_co, fa_33_s, fa_34_co, fa_34_s, fa_35_co, fa_35_s, fa_36_co, fa_36_s,
       fa_37_co, fa_37_s, fa_38_co, fa_38_s, fa_39_co, fa_39_s, fa_40_co, fa_40_s, fa_41_co, fa_41_s,
       fa_42_co, fa_42_s, fa_43_co, fa_43_s, fa_44_co, fa_44_s, fa_45_co, fa_45_s, fa_46_co, fa_46_s,
       fa_47_co, fa_47_s, fa_48_co, fa_48_s, ha_1_c, ha_2_c, ha_2_sum, ha_3_c, ha_4_c, ha_5_c, ha_6_c,
       ha_7_c, ha_8_c;

  and and_1 (and_1_out, A[7], B[7]);
  FA_2 fa_1 (.Co(P[15]), .S(P[14]), .Ci(fa_2_co), .A(and_1_out), .B(fa_3_co));
  and and_2 (and_2_out, A[7], B[6]);
  and and_3 (and_3_out, A[6], B[7]);
  FA_2 fa_2 (.Co(fa_2_co), .S(P[13]), .Ci(fa_4_co), .A(and_3_out), .B(fa_3_s));
  FA_2 fa_3 (.Co(fa_3_co), .S(fa_3_s), .Ci(fa_5_co), .A(and_2_out), .B(fa_6_co));
  and and_4 (and_4_out, A[5], B[7]);
  FA_2 fa_4 (.Co(fa_4_co), .S(P[12]), .Ci(fa_8_co), .A(and_4_out), .B(fa_5_s));
  and and_5 (and_5_out, A[7], B[5]);
  and and_6 (and_6_out, A[6], B[6]);
  FA_2 fa_5 (.Co(fa_5_co), .S(fa_5_s), .Ci(fa_7_co), .A(and_6_out), .B(fa_6_s));
  FA_2 fa_6 (.Co(fa_6_co), .S(fa_6_s), .Ci(fa_9_co), .A(and_5_out), .B(fa_11_co));
  and and_7 (and_7_out, A[5], B[6]);
  FA_2 fa_7 (.Co(fa_7_co), .S(fa_7_s), .Ci(fa_13_co), .A(and_7_out), .B(fa_9_s));
  and and_8 (and_8_out, A[4], B[7]);
  FA_2 fa_8 (.Co(fa_8_co), .S(P[11]), .Ci(fa_10_co), .A(and_8_out), .B(fa_7_s));
  and and_9 (and_9_out, A[7], B[4]);
  and and_10 (and_10_out, A[6], B[5]);
  FA_2 fa_9 (.Co(fa_9_co), .S(fa_9_s), .Ci(fa_12_co), .A(and_10_out), .B(fa_11_s));
  and and_11 (and_11_out, A[3], B[7]);
  FA_2 fa_10 (.Co(fa_10_co), .S(P[10]), .Ci(fa_16_co), .A(and_11_out), .B(fa_13_s));
  FA_2 fa_11 (.Co(fa_11_co), .S(fa_11_s), .Ci(fa_14_co), .A(and_9_out), .B(fa_17_co));
  and and_12 (and_12_out, A[5], B[5]);
  FA_2 fa_12 (.Co(fa_12_co), .S(fa_12_s), .Ci(fa_19_co), .A(and_12_out), .B(fa_14_s));
  and and_13 (and_13_out, A[4], B[6]);
  FA_2 fa_13 (.Co(fa_13_co), .S(fa_13_s), .Ci(fa_15_co), .A(and_13_out), .B(fa_12_s));
  and and_14 (and_14_out, A[7], B[3]);
  and and_15 (and_15_out, A[6], B[4]);
  FA_2 fa_14 (.Co(fa_14_co), .S(fa_14_s), .Ci(fa_18_co), .A(and_15_out), .B(fa_17_s));
  and and_16 (and_16_out, A[3], B[6]);
  FA_2 fa_15 (.Co(fa_15_co), .S(fa_15_s), .Ci(fa_23_co), .A(and_16_out), .B(fa_19_s));
  and and_17 (and_17_out, A[2], B[7]);
  FA_2 fa_16 (.Co(fa_16_co), .S(P[9]), .Ci(fa_20_co), .A(and_17_out), .B(fa_15_s));
  FA_2 fa_17 (.Co(fa_17_co), .S(fa_17_s), .Ci(fa_21_co), .A(and_14_out), .B(fa_24_co));
  and and_18 (and_18_out, A[5], B[4]);
  FA_2 fa_18 (.Co(fa_18_co), .S(fa_18_s), .Ci(fa_26_co), .A(and_18_out), .B(fa_21_s));
  and and_19 (and_19_out, A[4], B[5]);
  FA_2 fa_19 (.Co(fa_19_co), .S(fa_19_s), .Ci(fa_22_co), .A(and_19_out), .B(fa_18_s));
  and and_20 (and_20_out, A[1], B[7]);
  FA_2 fa_20 (.Co(fa_20_co), .S(P[8]), .Ci(ha_1_c), .A(and_20_out), .B(fa_23_s));
  and and_21 (and_21_out, A[7], B[2]);
  and and_22 (and_22_out, A[6], B[3]);
  FA_2 fa_21 (.Co(fa_21_co), .S(fa_21_s), .Ci(fa_25_co), .A(and_22_out), .B(fa_24_s));
  and and_23 (and_23_out, A[3], B[5]);
  FA_2 fa_22 (.Co(fa_22_co), .S(fa_22_s), .Ci(fa_30_co), .A(and_23_out), .B(fa_26_s));
  and and_24 (and_24_out, A[2], B[6]);
  FA_2 fa_23 (.Co(fa_23_co), .S(fa_23_s), .Ci(fa_27_co), .A(and_24_out), .B(fa_22_s));
  FA_2 fa_24 (.Co(fa_24_co), .S(fa_24_s), .Ci(fa_28_co), .A(and_21_out), .B(ha_2_c));
  and and_25 (and_25_out, A[5], B[3]);
  FA_2 fa_25 (.Co(fa_25_co), .S(fa_25_s), .Ci(fa_32_co), .A(and_25_out), .B(fa_28_s));
  and and_26 (and_26_out, A[4], B[4]);
  FA_2 fa_26 (.Co(fa_26_co), .S(fa_26_s), .Ci(fa_29_co), .A(and_26_out), .B(fa_25_s));
  and and_27 (and_27_out, A[1], B[6]);
  FA_2 fa_27 (.Co(fa_27_co), .S(fa_27_s), .Ci(ha_3_c), .A(and_27_out), .B(fa_30_s));
  and and_28 (and_28_out, A[0], B[7]);
  HA ha_1 (.C(ha_1_c), .SUM(P[7]), .A(and_28_out), .B(fa_27_s));
  and and_29 (and_29_out, A[7], B[1]);
  and and_30 (and_30_out, A[6], B[2]);
  FA_2 fa_28 (.Co(fa_28_co), .S(fa_28_s), .Ci(fa_31_co), .A(and_30_out), .B(ha_2_sum));
  and and_31 (and_31_out, A[3], B[4]);
  FA_2 fa_29 (.Co(fa_29_co), .S(fa_29_s), .Ci(fa_36_co), .A(and_31_out), .B(fa_32_s));
  and and_32 (and_32_out, A[2], B[5]);
  FA_2 fa_30 (.Co(fa_30_co), .S(fa_30_s), .Ci(fa_33_co), .A(and_32_out), .B(fa_29_s));
  HA ha_2 (.C(ha_2_c), .SUM(ha_2_sum), .A(and_29_out), .B(fa_34_co));
  and and_33 (and_33_out, A[5], B[2]);
  FA_2 fa_31 (.Co(fa_31_co), .S(fa_31_s), .Ci(fa_38_co), .A(and_33_out), .B(fa_34_s));
  and and_34 (and_34_out, A[4], B[3]);
  FA_2 fa_32 (.Co(fa_32_co), .S(fa_32_s), .Ci(fa_35_co), .A(and_34_out), .B(fa_31_s));
  and and_35 (and_35_out, A[1], B[5]);
  FA_2 fa_33 (.Co(fa_33_co), .S(fa_33_s), .Ci(ha_4_c), .A(and_35_out), .B(fa_36_s));
  and and_36 (and_36_out, A[0], B[6]);
  HA ha_3 (.C(ha_3_c), .SUM(P[6]), .A(and_36_out), .B(fa_33_s));
  and and_37 (and_37_out, A[6], B[1]);
  FA_2 fa_34 (.Co(fa_34_co), .S(fa_34_s), .Ci(fa_37_co), .A(and_37_out), .B(and_40_out));
  and and_38 (and_38_out, A[3], B[3]);
  FA_2 fa_35 (.Co(fa_35_co), .S(fa_35_s), .Ci(fa_41_co), .A(and_38_out), .B(fa_38_s));
  and and_39 (and_39_out, A[2], B[4]);
  FA_2 fa_36 (.Co(fa_36_co), .S(fa_36_s), .Ci(fa_39_co), .A(and_39_out), .B(fa_35_s));
  and and_40 (and_40_out, A[7], B[0]);
  and and_41 (and_41_out, A[5], B[1]);
  FA_2 fa_37 (.Co(fa_37_co), .S(fa_37_s), .Ci(fa_42_co), .A(and_41_out), .B(and_45_out));
  and and_42 (and_42_out, A[4], B[2]);
  FA_2 fa_38 (.Co(fa_38_co), .S(fa_38_s), .Ci(fa_40_co), .A(and_42_out), .B(fa_37_s));
  and and_43 (and_43_out, A[1], B[4]);
  FA_2 fa_39 (.Co(fa_39_co), .S(fa_39_s), .Ci(ha_5_c), .A(and_43_out), .B(fa_41_s));
  and and_44 (and_44_out, A[0], B[5]);
  HA ha_4 (.C(ha_4_c), .SUM(P[5]), .A(and_44_out), .B(fa_39_s));
  and and_45 (and_45_out, A[6], B[0]);
  and and_46 (and_46_out, A[3], B[2]);
  FA_2 fa_40 (.Co(fa_40_co), .S(fa_40_s), .Ci(fa_45_co), .A(and_46_out), .B(fa_42_s));
  and and_47 (and_47_out, A[2], B[3]);
  FA_2 fa_41 (.Co(fa_41_co), .S(fa_41_s), .Ci(fa_43_co), .A(and_47_out), .B(fa_40_s));
  and and_48 (and_48_out, A[4], B[1]);
  FA_2 fa_42 (.Co(fa_42_co), .S(fa_42_s), .Ci(fa_44_co), .A(and_48_out), .B(and_51_out));
  and and_49 (and_49_out, A[1], B[3]);
  FA_2 fa_43 (.Co(fa_43_co), .S(fa_43_s), .Ci(ha_6_c), .A(and_49_out), .B(fa_45_s));
  and and_50 (and_50_out, A[0], B[4]);
  HA ha_5 (.C(ha_5_c), .SUM(P[4]), .A(and_50_out), .B(fa_43_s));
  and and_51 (and_51_out, A[5], B[0]);
  and and_52 (and_52_out, A[3], B[1]);
  FA_2 fa_44 (.Co(fa_44_co), .S(fa_44_s), .Ci(fa_47_co), .A(and_52_out), .B(and_54_out));
  and and_53 (and_53_out, A[2], B[2]);
  FA_2 fa_45 (.Co(fa_45_co), .S(fa_45_s), .Ci(fa_46_co), .A(and_53_out), .B(fa_44_s));
  and and_54 (and_54_out, A[4], B[0]);
  and and_55 (and_55_out, A[1], B[2]);
  FA_2 fa_46 (.Co(fa_46_co), .S(fa_46_s), .Ci(ha_7_c), .A(and_55_out), .B(fa_47_s));
  and and_56 (and_56_out, A[0], B[3]);
  HA ha_6 (.C(ha_6_c), .SUM(P[3]), .A(and_56_out), .B(fa_46_s));
  and and_57 (and_57_out, A[2], B[1]);
  FA_2 fa_47 (.Co(fa_47_co), .S(fa_47_s), .Ci(fa_48_co), .A(and_57_out), .B(and_58_out));
  and and_58 (and_58_out, A[3], B[0]);
  and and_59 (and_59_out, A[1], B[1]);
  FA_2 fa_48 (.Co(fa_48_co), .S(fa_48_s), .Ci(ha_8_c), .A(and_59_out), .B(and_61_out));
  and and_60 (and_60_out, A[0], B[2]);
  HA ha_7 (.C(ha_7_c), .SUM(P[2]), .A(and_60_out), .B(fa_48_s));
  and and_61 (and_61_out, A[2], B[0]);
  and and_62 (and_62_out, A[0], B[1]);
  HA ha_8 (.C(ha_8_c), .SUM(P[1]), .A(and_62_out), .B(and_63_out));
  and and_63 (and_63_out, A[1], B[0]);
  and and_64 (P[0], A[0], B[0]);
endmodule

module _8_bit_Divider (
  input  [7:0] A,
  input  [7:0] B,
  output [7:0] Q,
  output [7:0] R
);

  wire fa_2_co, fa_2_s, fa_4_co, fa_4_s, fa_5_co, fa_5_s, fa_7_co, fa_7_s, fa_8_co, fa_8_s, fa_9_co, fa_9_s,
       fa_11_co, fa_11_s, fa_12_co, fa_12_s, fa_13_co, fa_13_s, fa_14_co, fa_14_s, fa_16_co, fa_16_s,
       fa_17_co, fa_17_s, fa_18_co, fa_18_s, fa_19_co, fa_19_s, fa_20_co, fa_20_s, fa_22_co, fa_22_s,
       fa_23_co, fa_23_s, fa_24_co, fa_24_s, fa_25_co, fa_25_s, fa_26_co, fa_26_s, fa_27_co, fa_27_s,
       fa_29_co, fa_29_s, fa_30_co, fa_30_s, fa_31_co, fa_31_s, fa_32_co, fa_32_s, fa_33_co, fa_33_s,
       fa_34_co, fa_34_s, fa_35_co, fa_35_s, fa_36_s, fa_37_co, fa_37_s, fa_38_co, fa_38_s, fa_39_co,
       fa_39_s, fa_40_co, fa_40_s, fa_41_co, fa_41_s, fa_42_co, fa_42_s, fa_43_co, fa_43_s, fa_44_co,
       fa_44_s, fa_45_co, fa_45_s, fa_46_co, fa_46_s, fa_47_co, fa_47_s, fa_48_co, fa_48_s, fa_49_co,
       fa_49_s, fa_50_co, fa_50_s, fa_51_co, fa_51_s, fa_52_co, fa_52_s, fa_53_co, fa_53_s, fa_54_co,
       fa_54_s, fa_55_co, fa_55_s, fa_56_co, fa_56_s, fa_57_co, fa_57_s, fa_58_co, fa_58_s, fa_59_co,
       fa_59_s, fa_60_co, fa_60_s, fa_61_co, fa_61_s, fa_62_co, fa_62_s, fa_63_co, fa_63_s, fa_64_co,
       fa_64_s, multiplexer_1_out, multiplexer_2_out, multiplexer_3_out, multiplexer_4_out,
       multiplexer_5_out, multiplexer_6_out, multiplexer_7_out, multiplexer_8_out, multiplexer_9_out,
       multiplexer_10_out, multiplexer_11_out, multiplexer_12_out, multiplexer_13_out, multiplexer_14_out,
       multiplexer_15_out, multiplexer_16_out, multiplexer_17_out, multiplexer_18_out, multiplexer_19_out,
       multiplexer_20_out, multiplexer_21_out, multiplexer_22_out, multiplexer_23_out, multiplexer_24_out,
       multiplexer_25_out, multiplexer_26_out, multiplexer_27_out, multiplexer_28_out, multiplexer_30_out,
       multiplexer_31_out, multiplexer_32_out, multiplexer_33_out, multiplexer_34_out, multiplexer_35_out,
       multiplexer_36_out, multiplexer_37_out, multiplexer_38_out, multiplexer_40_out, multiplexer_41_out,
       multiplexer_42_out, multiplexer_43_out, multiplexer_45_out, multiplexer_46_out, multiplexer_47_out,
       multiplexer_48_out, multiplexer_50_out, multiplexer_51_out, multiplexer_53_out, multiplexer_55_out,
       not_1_out, not_2_out, not_3_out, not_4_out, not_5_out, not_6_out, not_7_out, not_8_out,
       pull_resistor_1_node;

  Pull_Resistor pull_resistor_1 (.node(pull_resistor_1_node));
  FA_2 fa_1 (.Co(Q[7]), .Ci(fa_2_co), .A(pull_resistor_1_node), .B(not_1_out));  // open: S
  not not_1 (not_1_out, B[7]);
  not not_2 (not_2_out, B[6]);
  FA_2 fa_2 (.Co(fa_2_co), .S(fa_2_s), .Ci(fa_4_co), .A(pull_resistor_1_node), .B(not_2_out));
  Multiplexer #(.enable("false")) multiplexer_1 (
    .in0(pull_resistor_1_node), .in1(fa_2_s), .out(multiplexer_1_out), .sel(Q[7]));
  FA_2 fa_3 (.Co(Q[6]), .Ci(fa_5_co), .A(multiplexer_1_out), .B(not_1_out));  // open: S
  not not_3 (not_3_out, B[5]);
  FA_2 fa_4 (.Co(fa_4_co), .S(fa_4_s), .Ci(fa_7_co), .A(pull_resistor_1_node), .B(not_3_out));
  Multiplexer #(.enable("false")) multiplexer_2 (
    .in0(pull_resistor_1_node), .in1(fa_4_s), .out(multiplexer_2_out), .sel(Q[7]));
  FA_2 fa_5 (.Co(fa_5_co), .S(fa_5_s), .Ci(fa_8_co), .A(multiplexer_2_out), .B(not_2_out));
  Multiplexer #(.enable("false")) multiplexer_3 (
    .in0(multiplexer_2_out), .in1(fa_5_s), .out(multiplexer_3_out), .sel(Q[6]));
  FA_2 fa_6 (.Co(Q[5]), .Ci(fa_9_co), .A(multiplexer_3_out), .B(not_1_out));  // open: S
  not not_4 (not_4_out, B[4]);
  FA_2 fa_7 (.Co(fa_7_co), .S(fa_7_s), .Ci(fa_11_co), .A(pull_resistor_1_node), .B(not_4_out));
  Multiplexer #(.enable("false")) multiplexer_4 (
    .in0(pull_resistor_1_node), .in1(fa_7_s), .out(multiplexer_4_out), .sel(Q[7]));
  FA_2 fa_8 (.Co(fa_8_co), .S(fa_8_s), .Ci(fa_12_co), .A(multiplexer_4_out), .B(not_3_out));
  Multiplexer #(.enable("false")) multiplexer_5 (
    .in0(multiplexer_4_out), .in1(fa_8_s), .out(multiplexer_5_out), .sel(Q[6]));
  FA_2 fa_9 (.Co(fa_9_co), .S(fa_9_s), .Ci(fa_13_co), .A(multiplexer_5_out), .B(not_2_out));
  Multiplexer #(.enable("false")) multiplexer_6 (
    .in0(multiplexer_5_out), .in1(fa_9_s), .out(multiplexer_6_out), .sel(Q[5]));
  FA_2 fa_10 (.Co(Q[4]), .Ci(fa_14_co), .A(multiplexer_6_out), .B(not_1_out));  // open: S
  not not_5 (not_5_out, B[3]);
  FA_2 fa_11 (.Co(fa_11_co), .S(fa_11_s), .Ci(fa_16_co), .A(pull_resistor_1_node), .B(not_5_out));
  Multiplexer #(.enable("false")) multiplexer_7 (
    .in0(pull_resistor_1_node), .in1(fa_11_s), .out(multiplexer_7_out), .sel(Q[7]));
  FA_2 fa_12 (.Co(fa_12_co), .S(fa_12_s), .Ci(fa_17_co), .A(multiplexer_7_out), .B(not_4_out));
  Multiplexer #(.enable("false")) multiplexer_8 (
    .in0(multiplexer_7_out), .in1(fa_12_s), .out(multiplexer_8_out), .sel(Q[6]));
  FA_2 fa_13 (.Co(fa_13_co), .S(fa_13_s), .Ci(fa_18_co), .A(multiplexer_8_out), .B(not_3_out));
  Multiplexer #(.enable("false")) multiplexer_9 (
    .in0(multiplexer_8_out), .in1(fa_13_s), .out(multiplexer_9_out), .sel(Q[5]));
  FA_2 fa_14 (.Co(fa_14_co), .S(fa_14_s), .Ci(fa_19_co), .A(multiplexer_9_out), .B(not_2_out));
  Multiplexer #(.enable("false")) multiplexer_10 (
    .in0(multiplexer_9_out), .in1(fa_14_s), .out(multiplexer_10_out), .sel(Q[4]));
  FA_2 fa_15 (.Co(Q[3]), .Ci(fa_20_co), .A(multiplexer_10_out), .B(not_1_out));  // open: S
  not not_6 (not_6_out, B[2]);
  FA_2 fa_16 (.Co(fa_16_co), .S(fa_16_s), .Ci(fa_22_co), .A(pull_resistor_1_node), .B(not_6_out));
  Multiplexer #(.enable("false")) multiplexer_11 (
    .in0(pull_resistor_1_node), .in1(fa_16_s), .out(multiplexer_11_out), .sel(Q[7]));
  FA_2 fa_17 (.Co(fa_17_co), .S(fa_17_s), .Ci(fa_23_co), .A(multiplexer_11_out), .B(not_5_out));
  Multiplexer #(.enable("false")) multiplexer_12 (
    .in0(multiplexer_11_out), .in1(fa_17_s), .out(multiplexer_12_out), .sel(Q[6]));
  FA_2 fa_18 (.Co(fa_18_co), .S(fa_18_s), .Ci(fa_24_co), .A(multiplexer_12_out), .B(not_4_out));
  Multiplexer #(.enable("false")) multiplexer_13 (
    .in0(multiplexer_12_out), .in1(fa_18_s), .out(multiplexer_13_out), .sel(Q[5]));
  FA_2 fa_19 (.Co(fa_19_co), .S(fa_19_s), .Ci(fa_25_co), .A(multiplexer_13_out), .B(not_3_out));
  Multiplexer #(.enable("false")) multiplexer_14 (
    .in0(multiplexer_13_out), .in1(fa_19_s), .out(multiplexer_14_out), .sel(Q[4]));
  FA_2 fa_20 (.Co(fa_20_co), .S(fa_20_s), .Ci(fa_26_co), .A(multiplexer_14_out), .B(not_2_out));
  Multiplexer #(.enable("false")) multiplexer_15 (
    .in0(multiplexer_14_out), .in1(fa_20_s), .out(multiplexer_15_out), .sel(Q[3]));
  FA_2 fa_21 (.Co(Q[2]), .Ci(fa_27_co), .A(multiplexer_15_out), .B(not_1_out));  // open: S
  not not_7 (not_7_out, B[1]);
  FA_2 fa_22 (.Co(fa_22_co), .S(fa_22_s), .Ci(fa_29_co), .A(pull_resistor_1_node), .B(not_7_out));
  Multiplexer #(.enable("false")) multiplexer_16 (
    .in0(pull_resistor_1_node), .in1(fa_22_s), .out(multiplexer_16_out), .sel(Q[7]));
  FA_2 fa_23 (.Co(fa_23_co), .S(fa_23_s), .Ci(fa_30_co), .A(multiplexer_16_out), .B(not_6_out));
  Multiplexer #(.enable("false")) multiplexer_17 (
    .in0(multiplexer_16_out), .in1(fa_23_s), .out(multiplexer_17_out), .sel(Q[6]));
  FA_2 fa_24 (.Co(fa_24_co), .S(fa_24_s), .Ci(fa_31_co), .A(multiplexer_17_out), .B(not_5_out));
  Multiplexer #(.enable("false")) multiplexer_18 (
    .in0(multiplexer_17_out), .in1(fa_24_s), .out(multiplexer_18_out), .sel(Q[5]));
  FA_2 fa_25 (.Co(fa_25_co), .S(fa_25_s), .Ci(fa_32_co), .A(multiplexer_18_out), .B(not_4_out));
  Multiplexer #(.enable("false")) multiplexer_19 (
    .in0(multiplexer_18_out), .in1(fa_25_s), .out(multiplexer_19_out), .sel(Q[4]));
  FA_2 fa_26 (.Co(fa_26_co), .S(fa_26_s), .Ci(fa_33_co), .A(multiplexer_19_out), .B(not_3_out));
  Multiplexer #(.enable("false")) multiplexer_20 (
    .in0(multiplexer_19_out), .in1(fa_26_s), .out(multiplexer_20_out), .sel(Q[3]));
  FA_2 fa_27 (.Co(fa_27_co), .S(fa_27_s), .Ci(fa_34_co), .A(multiplexer_20_out), .B(not_2_out));
  Multiplexer #(.enable("false")) multiplexer_21 (
    .in0(multiplexer_20_out), .in1(fa_27_s), .out(multiplexer_21_out), .sel(Q[2]));
  FA_2 fa_28 (.Co(Q[1]), .Ci(fa_35_co), .A(multiplexer_21_out), .B(not_1_out));  // open: S
  not not_8 (not_8_out, B[0]);
  FA_2 fa_29 (.Co(fa_29_co), .S(fa_29_s), .Ci(1'b1), .A(A[7]), .B(not_8_out));
  Multiplexer #(.enable("false")) multiplexer_22 (.in0(A[7]), .in1(fa_29_s), .out(multiplexer_22_out), .sel(Q[7]));
  FA_2 fa_30 (.Co(fa_30_co), .S(fa_30_s), .Ci(fa_37_co), .A(multiplexer_22_out), .B(not_7_out));
  Multiplexer #(.enable("false")) multiplexer_23 (
    .in0(multiplexer_22_out), .in1(fa_30_s), .out(multiplexer_23_out), .sel(Q[6]));
  FA_2 fa_31 (.Co(fa_31_co), .S(fa_31_s), .Ci(fa_38_co), .A(multiplexer_23_out), .B(not_6_out));
  Multiplexer #(.enable("false")) multiplexer_24 (
    .in0(multiplexer_23_out), .in1(fa_31_s), .out(multiplexer_24_out), .sel(Q[5]));
  FA_2 fa_32 (.Co(fa_32_co), .S(fa_32_s), .Ci(fa_39_co), .A(multiplexer_24_out), .B(not_5_out));
  Multiplexer #(.enable("false")) multiplexer_25 (
    .in0(multiplexer_24_out), .in1(fa_32_s), .out(multiplexer_25_out), .sel(Q[4]));
  FA_2 fa_33 (.Co(fa_33_co), .S(fa_33_s), .Ci(fa_40_co), .A(multiplexer_25_out), .B(not_4_out));
  Multiplexer #(.enable("false")) multiplexer_26 (
    .in0(multiplexer_25_out), .in1(fa_33_s), .out(multiplexer_26_out), .sel(Q[3]));
  FA_2 fa_34 (.Co(fa_34_co), .S(fa_34_s), .Ci(fa_41_co), .A(multiplexer_26_out), .B(not_3_out));
  Multiplexer #(.enable("false")) multiplexer_27 (
    .in0(multiplexer_26_out), .in1(fa_34_s), .out(multiplexer_27_out), .sel(Q[2]));
  FA_2 fa_35 (.Co(fa_35_co), .S(fa_35_s), .Ci(fa_42_co), .A(multiplexer_27_out), .B(not_2_out));
  Multiplexer #(.enable("false")) multiplexer_28 (
    .in0(multiplexer_27_out), .in1(fa_35_s), .out(multiplexer_28_out), .sel(Q[1]));
  FA_2 fa_36 (.Co(Q[0]), .S(fa_36_s), .Ci(fa_43_co), .A(multiplexer_28_out), .B(not_1_out));
  Multiplexer #(.enable("false")) multiplexer_29 (.in0(multiplexer_28_out), .in1(fa_36_s), .out(R[7]), .sel(Q[0]));
  FA_2 fa_37 (.Co(fa_37_co), .S(fa_37_s), .Ci(1'b1), .A(A[6]), .B(not_8_out));
  Multiplexer #(.enable("false")) multiplexer_30 (.in0(A[6]), .in1(fa_37_s), .out(multiplexer_30_out), .sel(Q[6]));
  FA_2 fa_38 (.Co(fa_38_co), .S(fa_38_s), .Ci(fa_44_co), .A(multiplexer_30_out), .B(not_7_out));
  Multiplexer #(.enable("false")) multiplexer_31 (
    .in0(multiplexer_30_out), .in1(fa_38_s), .out(multiplexer_31_out), .sel(Q[5]));
  FA_2 fa_39 (.Co(fa_39_co), .S(fa_39_s), .Ci(fa_45_co), .A(multiplexer_31_out), .B(not_6_out));
  Multiplexer #(.enable("false")) multiplexer_32 (
    .in0(multiplexer_31_out), .in1(fa_39_s), .out(multiplexer_32_out), .sel(Q[4]));
  FA_2 fa_40 (.Co(fa_40_co), .S(fa_40_s), .Ci(fa_46_co), .A(multiplexer_32_out), .B(not_5_out));
  Multiplexer #(.enable("false")) multiplexer_33 (
    .in0(multiplexer_32_out), .in1(fa_40_s), .out(multiplexer_33_out), .sel(Q[3]));
  FA_2 fa_41 (.Co(fa_41_co), .S(fa_41_s), .Ci(fa_47_co), .A(multiplexer_33_out), .B(not_4_out));
  FA_2 fa_42 (.Co(fa_42_co), .S(fa_42_s), .Ci(fa_51_co), .A(multiplexer_37_out), .B(not_3_out));
  FA_2 fa_43 (.Co(fa_43_co), .S(fa_43_s), .Ci(fa_52_co), .A(multiplexer_38_out), .B(not_2_out));
  FA_2 fa_44 (.Co(fa_44_co), .S(fa_44_s), .Ci(1'b1), .A(A[5]), .B(not_8_out));
  Multiplexer #(.enable("false")) multiplexer_34 (.in0(A[5]), .in1(fa_44_s), .out(multiplexer_34_out), .sel(Q[5]));
  FA_2 fa_45 (.Co(fa_45_co), .S(fa_45_s), .Ci(fa_48_co), .A(multiplexer_34_out), .B(not_7_out));
  Multiplexer #(.enable("false")) multiplexer_35 (
    .in0(multiplexer_34_out), .in1(fa_45_s), .out(multiplexer_35_out), .sel(Q[4]));
  FA_2 fa_46 (.Co(fa_46_co), .S(fa_46_s), .Ci(fa_49_co), .A(multiplexer_35_out), .B(not_6_out));
  Multiplexer #(.enable("false")) multiplexer_36 (
    .in0(multiplexer_35_out), .in1(fa_46_s), .out(multiplexer_36_out), .sel(Q[3]));
  FA_2 fa_47 (.Co(fa_47_co), .S(fa_47_s), .Ci(fa_50_co), .A(multiplexer_36_out), .B(not_5_out));
  Multiplexer #(.enable("false")) multiplexer_37 (
    .in0(multiplexer_33_out), .in1(fa_41_s), .out(multiplexer_37_out), .sel(Q[2]));
  Multiplexer #(.enable("false")) multiplexer_38 (
    .in0(multiplexer_37_out), .in1(fa_42_s), .out(multiplexer_38_out), .sel(Q[1]));
  Multiplexer #(.enable("false")) multiplexer_39 (.in0(multiplexer_38_out), .in1(fa_43_s), .out(R[6]), .sel(Q[0]));
  FA_2 fa_48 (.Co(fa_48_co), .S(fa_48_s), .Ci(1'b1), .A(A[4]), .B(not_8_out));
  Multiplexer #(.enable("false")) multiplexer_40 (.in0(A[4]), .in1(fa_48_s), .out(multiplexer_40_out), .sel(Q[4]));
  FA_2 fa_49 (.Co(fa_49_co), .S(fa_49_s), .Ci(fa_53_co), .A(multiplexer_40_out), .B(not_7_out));
  Multiplexer #(.enable("false")) multiplexer_41 (
    .in0(multiplexer_40_out), .in1(fa_49_s), .out(multiplexer_41_out), .sel(Q[3]));
  FA_2 fa_50 (.Co(fa_50_co), .S(fa_50_s), .Ci(fa_54_co), .A(multiplexer_41_out), .B(not_6_out));
  Multiplexer #(.enable("false")) multiplexer_42 (
    .in0(multiplexer_36_out), .in1(fa_47_s), .out(multiplexer_42_out), .sel(Q[2]));
  FA_2 fa_51 (.Co(fa_51_co), .S(fa_51_s), .Ci(fa_55_co), .A(multiplexer_42_out), .B(not_4_out));
  Multiplexer #(.enable("false")) multiplexer_43 (
    .in0(multiplexer_42_out), .in1(fa_51_s), .out(multiplexer_43_out), .sel(Q[1]));
  FA_2 fa_52 (.Co(fa_52_co), .S(fa_52_s), .Ci(fa_56_co), .A(multiplexer_43_out), .B(not_3_out));
  Multiplexer #(.enable("false")) multiplexer_44 (.in0(multiplexer_43_out), .in1(fa_52_s), .out(R[5]), .sel(Q[0]));
  FA_2 fa_53 (.Co(fa_53_co), .S(fa_53_s), .Ci(1'b1), .A(A[3]), .B(not_8_out));
  Multiplexer #(.enable("false")) multiplexer_45 (.in0(A[3]), .in1(fa_53_s), .out(multiplexer_45_out), .sel(Q[3]));
  FA_2 fa_54 (.Co(fa_54_co), .S(fa_54_s), .Ci(fa_57_co), .A(multiplexer_45_out), .B(not_7_out));
  Multiplexer #(.enable("false")) multiplexer_46 (
    .in0(multiplexer_41_out), .in1(fa_50_s), .out(multiplexer_46_out), .sel(Q[2]));
  Multiplexer #(.enable("false")) multiplexer_47 (
    .in0(multiplexer_45_out), .in1(fa_54_s), .out(multiplexer_47_out), .sel(Q[2]));
  FA_2 fa_55 (.Co(fa_55_co), .S(fa_55_s), .Ci(fa_58_co), .A(multiplexer_46_out), .B(not_5_out));
  Multiplexer #(.enable("false")) multiplexer_48 (
    .in0(multiplexer_46_out), .in1(fa_55_s), .out(multiplexer_48_out), .sel(Q[1]));
  FA_2 fa_56 (.Co(fa_56_co), .S(fa_56_s), .Ci(fa_59_co), .A(multiplexer_48_out), .B(not_4_out));
  Multiplexer #(.enable("false")) multiplexer_49 (.in0(multiplexer_48_out), .in1(fa_56_s), .out(R[4]), .sel(Q[0]));
  FA_2 fa_57 (.Co(fa_57_co), .S(fa_57_s), .Ci(1'b1), .A(A[2]), .B(not_8_out));
  Multiplexer #(.enable("false")) multiplexer_50 (.in0(A[2]), .in1(fa_57_s), .out(multiplexer_50_out), .sel(Q[2]));
  FA_2 fa_58 (.Co(fa_58_co), .S(fa_58_s), .Ci(fa_60_co), .A(multiplexer_47_out), .B(not_6_out));
  Multiplexer #(.enable("false")) multiplexer_51 (
    .in0(multiplexer_47_out), .in1(fa_58_s), .out(multiplexer_51_out), .sel(Q[1]));
  FA_2 fa_59 (.Co(fa_59_co), .S(fa_59_s), .Ci(fa_62_co), .A(multiplexer_51_out), .B(not_5_out));
  Multiplexer #(.enable("false")) multiplexer_52 (.in0(multiplexer_51_out), .in1(fa_59_s), .out(R[3]), .sel(Q[0]));
  FA_2 fa_60 (.Co(fa_60_co), .S(fa_60_s), .Ci(fa_61_co), .A(multiplexer_50_out), .B(not_7_out));
  FA_2 fa_61 (.Co(fa_61_co), .S(fa_61_s), .Ci(1'b1), .A(A[1]), .B(not_8_out));
  Multiplexer #(.enable("false")) multiplexer_53 (
    .in0(multiplexer_50_out), .in1(fa_60_s), .out(multiplexer_53_out), .sel(Q[1]));
  FA_2 fa_62 (.Co(fa_62_co), .S(fa_62_s), .Ci(fa_63_co), .A(multiplexer_53_out), .B(not_6_out));
  Multiplexer #(.enable("false")) multiplexer_54 (.in0(multiplexer_53_out), .in1(fa_62_s), .out(R[2]), .sel(Q[0]));
  Multiplexer #(.enable("false")) multiplexer_55 (.in0(A[1]), .in1(fa_61_s), .out(multiplexer_55_out), .sel(Q[1]));
  FA_2 fa_63 (.Co(fa_63_co), .S(fa_63_s), .Ci(fa_64_co), .A(multiplexer_55_out), .B(not_7_out));
  FA_2 fa_64 (.Co(fa_64_co), .S(fa_64_s), .Ci(1'b1), .A(A[0]), .B(not_8_out));
  Multiplexer #(.enable("false")) multiplexer_56 (.in0(multiplexer_55_out), .in1(fa_63_s), .out(R[1]), .sel(Q[0]));
  Multiplexer #(.enable("false")) multiplexer_57 (.in0(A[0]), .in1(fa_64_s), .out(R[0]), .sel(Q[0]));
endmodule

module _8bit_LSR___ASR (
  input  [7:0] A,
  input  ASR,
  input  [2:0] n,
  output [7:0] out_4
);

  Multiplexer #(.enable("false"), .select(3), .width(8)) multiplexer_1 (
    .in0(A), .in1({ASR, A[7:1]}), .in2({{2{ASR}}, A[7:2]}), .in3({{3{ASR}}, A[7:3]}),
    .in4({{4{ASR}}, A[7:4]}), .in5({{5{ASR}}, A[7:5]}), .in6({{6{ASR}}, A[7:6]}), .in7({{7{ASR}}, A[7]}),
    .out(out_4), .sel(n));
endmodule

module _8bit_LSL (
  input  [7:0] A,
  input  [2:0] n,
  output [7:0] out_3
);

  wire [0:0] pull_resistor_7_node;
  wire [1:1] pull_resistor_6_node;
  wire [2:2] pull_resistor_5_node;
  wire [3:3] pull_resistor_4_node;
  wire [4:4] pull_resistor_3_node;
  wire [5:5] pull_resistor_2_node;
  wire [6:6] pull_resistor_1_node;

  Pull_Resistor pull_resistor_1 (.node(pull_resistor_1_node[6]));
  Pull_Resistor pull_resistor_2 (.node(pull_resistor_2_node[5]));
  Pull_Resistor pull_resistor_3 (.node(pull_resistor_3_node[4]));
  Pull_Resistor pull_resistor_4 (.node(pull_resistor_4_node[3]));
  Pull_Resistor pull_resistor_5 (.node(pull_resistor_5_node[2]));
  Pull_Resistor pull_resistor_6 (.node(pull_resistor_6_node[1]));
  Pull_Resistor pull_resistor_7 (.node(pull_resistor_7_node[0]));
  Multiplexer #(.enable("false"), .select(3), .width(8)) multiplexer_1 (
    .in0(A), .in1({A[6:0], pull_resistor_7_node[0]}),
    .in2({{2{A[4]}}, A[3:0], {2{pull_resistor_6_node[1]}}}), .in3({A[4:0], {3{pull_resistor_5_node[2]}}}),
    .in4({A[3:0], {4{pull_resistor_4_node[3]}}}), .in5({A[2:0], {5{pull_resistor_3_node[4]}}}),
    .in6({A[1:0], {6{pull_resistor_2_node[5]}}}), .in7({A[0], {7{pull_resistor_1_node[6]}}}), .out(out_3),
    .sel(n));
endmodule

module _8bit_ROR (
  input  [7:0] A,
  input  [2:0] n,
  output [7:0] out_3
);

  Multiplexer #(.enable("false"), .select(3), .width(8)) multiplexer_1 (
    .in0(A), .in1({A[0], A[7:1]}), .in2({A[1:0], A[7:2]}), .in3({A[2:0], A[7:3]}), .in4({A[3:0], A[7:4]}),
    .in5({A[4:0], A[7:5]}), .in6({A[5:0], A[7:6]}), .in7({A[6:0], A[7]}), .out(out_3), .sel(n));
endmodule

module _8bit_ROL (
  input  [7:0] A,
  input  [2:0] n,
  output [7:0] out_3
);

  Multiplexer #(.enable("false"), .select(3), .width(8)) multiplexer_1 (
    .in0(A), .in1({A[6:0], A[7]}), .in2({A[5:0], A[7:6]}), .in3({A[4:0], A[7:5]}), .in4({A[3:0], A[7:4]}),
    .in5({A[2:0], A[7:3]}), .in6({A[1:0], A[7:2]}), .in7({A[0], A[7:1]}), .out(out_3), .sel(n));
endmodule

module _8bit_ALU (
  input  [7:0] in_1,
  input  [7:0] in_2,
  input  in_3,
  input  in_4,
  input  in_5,
  input  in_6,
  output out_7,
  output out_8,
  output out_9,
  output out_10,
  output [7:0] out_11,
  output [7:0] out_12,
  output [7:0] out_13,
  output [7:0] out_14
);

  wire [7:0] multiplexer_1_out;

  Multiplexer #(.enable("false"), .width(8)) multiplexer_1 (
    .in0({8{1'b0}}), .in1(in_1), .out(multiplexer_1_out), .sel(in_3));
  _8_bit_Adder u_8_bit_adder_1 (
    .Z(out_10), .C(out_7), .N(out_8), .V(out_9), .XOR(out_12), .OR(out_13), .SUM(out_14), .AND(out_11),
    .B_inv(in_4), .A_inv(in_5), .A(in_2), .B(multiplexer_1_out), .Cin(in_6));
  // _8_bit_Divider 8_bit_divider_1: pin names not known
  _8_bit_Multiplier u_8_bit_multiplier_1 ();  // open: P, A, B
  // _8bit_LSR___ASR 8bit_lsr_asr_1: pin names not known
  // _8bit_LSL 8bit_lsl_1: pin names not known
  // _8bit_ROR 8bit_ror_1: pin names not known
  // _8bit_ROL 8bit_rol_1: pin names not known
endmodule
