// Logisim project 8bit_Divider.circ as structural Verilog: 3 circuits, main circuit main
module main (
  input  [7:0] A,
  input  [7:0] B,
  output [7:0] Q,
  output [7:0] R
);

  wire fa_2_co, fa_2_s, fa_4_co, fa_4_s, fa_5_co, fa_5_s, fa_7_co, fa_7_s, fa_8_co, fa_8_s, fa_9_co, fa_9_s,
       fa_11_co, fa_11_s, fa_12_co, fa_12_s, fa_13_co, fa_13_s, fa_14_co, fa_14_s, fa_16_co, fa_16_s,
       fa_17_co, fa_17_s, fa_18_co, fa_18_s, fa_19_co, fa_19_s, fa_20_co, fa_20_s, fa_22_co, fa_22_s,
       fa_23_co, fa_23_s, fa_24_co, fa_24_s, fa_25_co, fa_25_s, fa_26_co, fa_26_s, fa_27_co, fa_27_s,
       fa_29_co, fa_29_s, fa_30_co, fa_30_s, fa_31_co, fa_31_s, fa_32_co, fa_32_s, fa_33_co, fa_33_s,
       fa_34_co, fa_34_s, fa_35_co, fa_35_s, fa_36_co, fa_36_s, fa_37_co, fa_37_s, fa_38_co, fa_38_s,
       fa_39_s, fa_40_co, fa_40_s, fa_41_co, fa_41_s, fa_42_co, fa_42_s, fa_43_co, fa_43_s, fa_44_co,
       fa_44_s, fa_45_co, fa_45_s, fa_46_co, fa_46_s, fa_47_co, fa_47_s, fa_48_co, fa_48_s, fa_49_co,
       fa_49_s, fa_50_co, fa_50_s, fa_51_co, fa_51_s, fa_52_co, fa_52_s, fa_53_co, fa_53_s, fa_54_co,
       fa_54_s, fa_55_co, fa_55_s, fa_56_co, fa_56_s, fa_57_co, fa_57_s, fa_58_co, fa_58_s, fa_59_co,
       fa_59_s, fa_60_co, fa_60_s, fa_61_co, fa_61_s, fa_62_co, fa_62_s, fa_63_co, fa_63_s, fa_64_co,
       fa_64_s, multiplexer_1_out, multiplexer_2_out, multiplexer_3_out, multiplexer_4_out,
       multiplexer_5_out, multiplexer_6_out, multiplexer_7_out, multiplexer_8_out, multiplexer_9_out,
       multiplexer_10_out, multiplexer_11_out, multiplexer_12_out, multiplexer_13_out, multiplexer_14_out,
       multiplexer_15_out, multiplexer_16_out, multiplexer_17_out, multiplexer_18_out, multiplexer_19_out,
       multiplexer_20_out, multiplexer_21_out, multiplexer_22_out, multiplexer_23_out, multiplexer_24_out,
       multiplexer_25_out, multiplexer_26_out, multiplexer_27_out, multiplexer_28_out, multiplexer_29_out,
       multiplexer_30_out, multiplexer_32_out, multiplexer_33_out, multiplexer_34_out, multiplexer_35_out,
       multiplexer_36_out, multiplexer_38_out, multiplexer_39_out, multiplexer_40_out, multiplexer_41_out,
       multiplexer_42_out, multiplexer_44_out, multiplexer_45_out, multiplexer_46_out, multiplexer_48_out,
       multiplexer_49_out, multiplexer_50_out, multiplexer_52_out, multiplexer_53_out, multiplexer_55_out,
       not_1_out, not_2_out, not_3_out, not_4_out, not_5_out, not_6_out, not_7_out, not_8_out,
       pull_resistor_1_node;

  Pull_Resistor pull_resistor_1 (.node(pull_resistor_1_node));
  not not_1 (not_1_out, B[7]);
  FA fa_1 (.Co(Q[7]), .Ci(fa_2_co), .A(pull_resistor_1_node), .B(not_1_out));  // open: S
  not not_2 (not_2_out, B[6]);
  FA fa_2 (.Co(fa_2_co), .S(fa_2_s), .Ci(fa_4_co), .A(pull_resistor_1_node), .B(not_2_out));
  Multiplexer #(.enable("false")) multiplexer_1 (
    .in0(pull_resistor_1_node), .in1(fa_2_s), .out(multiplexer_1_out), .sel(Q[7]));
  FA fa_3 (.Co(Q[6]), .Ci(fa_5_co), .A(multiplexer_1_out), .B(not_1_out));  // open: S
  not not_3 (not_3_out, B[5]);
  FA fa_4 (.Co(fa_4_co), .S(fa_4_s), .Ci(fa_7_co), .A(pull_resistor_1_node), .B(not_3_out));
  Multiplexer #(.enable("false")) multiplexer_2 (
    .in0(pull_resistor_1_node), .in1(fa_4_s), .out(multiplexer_2_out), .sel(Q[7]));
  FA fa_5 (.Co(fa_5_co), .S(fa_5_s), .Ci(fa_8_co), .A(multiplexer_2_out), .B(not_2_out));
  Multiplexer #(.enable("false")) multiplexer_3 (
    .in0(multiplexer_2_out), .in1(fa_5_s), .out(multiplexer_3_out), .sel(Q[6]));
  FA fa_6 (.Co(Q[5]), .Ci(fa_9_co), .A(multiplexer_3_out), .B(not_1_out));  // open: S
  not not_4 (not_4_out, B[4]);
  FA fa_7 (.Co(fa_7_co), .S(fa_7_s), .Ci(fa_11_co), .A(pull_resistor_1_node), .B(not_4_out));
  Multiplexer #(.enable("false")) multiplexer_4 (
    .in0(pull_resistor_1_node), .in1(fa_7_s), .out(multiplexer_4_out), .sel(Q[7]));
  FA fa_8 (.Co(fa_8_co), .S(fa_8_s), .Ci(fa_12_co), .A(multiplexer_4_out), .B(not_3_out));
  Multiplexer #(.enable("false")) multiplexer_5 (
    .in0(multiplexer_4_out), .in1(fa_8_s), .out(multiplexer_5_out), .sel(Q[6]));
  FA fa_9 (.Co(fa_9_co), .S(fa_9_s), .Ci(fa_13_co), .A(multiplexer_5_out), .B(not_2_out));
  Multiplexer #(.enable("false")) multiplexer_6 (
    .in0(multiplexer_5_out), .in1(fa_9_s), .out(multiplexer_6_out), .sel(Q[5]));
  FA fa_10 (.Co(Q[4]), .Ci(fa_14_co), .A(multiplexer_6_out), .B(not_1_out));  // open: S
  FA fa_11 (.Co(fa_11_co), .S(fa_11_s), .Ci(fa_16_co), .A(pull_resistor_1_node), .B(not_5_out));
  Multiplexer #(.enable("false")) multiplexer_7 (
    .in0(pull_resistor_1_node), .in1(fa_11_s), .out(multiplexer_7_out), .sel(Q[7]));
  FA fa_12 (.Co(fa_12_co), .S(fa_12_s), .Ci(fa_17_co), .A(multiplexer_7_out), .B(not_4_out));
  Multiplexer #(.enable("false")) multiplexer_8 (
    .in0(multiplexer_7_out), .in1(fa_12_s), .out(multiplexer_8_out), .sel(Q[6]));
  FA fa_13 (.Co(fa_13_co), .S(fa_13_s), .Ci(fa_18_co), .A(multiplexer_8_out), .B(not_3_out));
  Multiplexer #(.enable("false")) multiplexer_9 (
    .in0(multiplexer_8_out), .in1(fa_13_s), .out(multiplexer_9_out), .sel(Q[5]));
  FA fa_14 (.Co(fa_14_co), .S(fa_14_s), .Ci(fa_19_co), .A(multiplexer_9_out), .B(not_2_out));
  Multiplexer #(.enable("false")) multiplexer_10 (
    .in0(multiplexer_9_out), .in1(fa_14_s), .out(multiplexer_10_out), .sel(Q[4]));
  FA fa_15 (.Co(Q[3]), .Ci(fa_20_co), .A(multiplexer_10_out), .B(not_1_out));  // open: S
  not not_5 (not_5_out, B[3]);
  FA fa_16 (.Co(fa_16_co), .S(fa_16_s), .Ci(fa_22_co), .A(pull_resistor_1_node), .B(not_6_out));
  Multiplexer #(.enable("false")) multiplexer_11 (
    .in0(pull_resistor_1_node), .in1(fa_16_s), .out(multiplexer_11_out), .sel(Q[7]));
  FA fa_17 (.Co(fa_17_co), .S(fa_17_s), .Ci(fa_23_co), .A(multiplexer_11_out), .B(not_5_out));
  Multiplexer #(.enable("false")) multiplexer_12 (
    .in0(multiplexer_11_out), .in1(fa_17_s), .out(multiplexer_12_out), .sel(Q[6]));
  FA fa_18 (.Co(fa_18_co), .S(fa_18_s), .Ci(fa_24_co), .A(multiplexer_12_out), .B(not_4_out));
  Multiplexer #(.enable("false")) multiplexer_13 (
    .in0(multiplexer_12_out), .in1(fa_18_s), .out(multiplexer_13_out), .sel(Q[5]));
  FA fa_19 (.Co(fa_19_co), .S(fa_19_s), .Ci(fa_25_co), .A(multiplexer_13_out), .B(not_3_out));
  Multiplexer #(.enable("false")) multiplexer_14 (
    .in0(multiplexer_13_out), .in1(fa_19_s), .out(multiplexer_14_out), .sel(Q[4]));
  FA fa_20 (.Co(fa_20_co), .S(fa_20_s), .Ci(fa_26_co), .A(multiplexer_14_out), .B(not_2_out));
  Multiplexer #(.enable("false")) multiplexer_15 (
    .in0(multiplexer_14_out), .in1(fa_20_s), .out(multiplexer_15_out), .sel(Q[3]));
  FA fa_21 (.Co(Q[2]), .Ci(fa_27_co), .A(multiplexer_15_out), .B(not_1_out));  // open: S
  not not_6 (not_6_out, B[2]);
  FA fa_22 (.Co(fa_22_co), .S(fa_22_s), .Ci(fa_29_co), .A(pull_resistor_1_node), .B(not_7_out));
  Multiplexer #(.enable("false")) multiplexer_16 (
    .in0(pull_resistor_1_node), .in1(fa_22_s), .out(multiplexer_16_out), .sel(Q[7]));
  FA fa_23 (.Co(fa_23_co), .S(fa_23_s), .Ci(fa_30_co), .A(multiplexer_16_out), .B(not_6_out));
  Multiplexer #(.enable("false")) multiplexer_17 (
    .in0(multiplexer_16_out), .in1(fa_23_s), .out(multiplexer_17_out), .sel(Q[6]));
  FA fa_24 (.Co(fa_24_co), .S(fa_24_s), .Ci(fa_31_co), .A(multiplexer_17_out), .B(not_5_out));
  Multiplexer #(.enable("false")) multiplexer_18 (
    .in0(multiplexer_17_out), .in1(fa_24_s), .out(multiplexer_18_out), .sel(Q[5]));
  FA fa_25 (.Co(fa_25_co), .S(fa_25_s), .Ci(fa_32_co), .A(multiplexer_18_out), .B(not_4_out));
  FA fa_26 (.Co(fa_26_co), .S(fa_26_s), .Ci(fa_36_co), .A(multiplexer_22_out), .B(not_3_out));
  FA fa_27 (.Co(fa_27_co), .S(fa_27_s), .Ci(fa_37_co), .A(multiplexer_23_out), .B(not_2_out));
  FA fa_28 (.Co(Q[1]), .Ci(fa_38_co), .A(multiplexer_24_out), .B(not_1_out));  // open: S
  not not_7 (not_7_out, B[1]);
  not not_8 (not_8_out, B[0]);
  FA fa_29 (.Co(fa_29_co), .S(fa_29_s), .Ci(1'b1), .A(A[7]), .B(not_8_out));
  Multiplexer #(.enable("false")) multiplexer_19 (.in0(A[7]), .in1(fa_29_s), .out(multiplexer_19_out), .sel(Q[7]));
  FA fa_30 (.Co(fa_30_co), .S(fa_30_s), .Ci(fa_33_co), .A(multiplexer_19_out), .B(not_7_out));
  Multiplexer #(.enable("false")) multiplexer_20 (
    .in0(multiplexer_19_out), .in1(fa_30_s), .out(multiplexer_20_out), .sel(Q[6]));
  FA fa_31 (.Co(fa_31_co), .S(fa_31_s), .Ci(fa_34_co), .A(multiplexer_20_out), .B(not_6_out));
  Multiplexer #(.enable("false")) multiplexer_21 (
    .in0(multiplexer_20_out), .in1(fa_31_s), .out(multiplexer_21_out), .sel(Q[5]));
  FA fa_32 (.Co(fa_32_co), .S(fa_32_s), .Ci(fa_35_co), .A(multiplexer_21_out), .B(not_5_out));
  Multiplexer #(.enable("false")) multiplexer_22 (
    .in0(multiplexer_18_out), .in1(fa_25_s), .out(multiplexer_22_out), .sel(Q[4]));
  Multiplexer #(.enable("false")) multiplexer_23 (
    .in0(multiplexer_22_out), .in1(fa_26_s), .out(multiplexer_23_out), .sel(Q[3]));
  Multiplexer #(.enable("false")) multiplexer_24 (
    .in0(multiplexer_23_out), .in1(fa_27_s), .out(multiplexer_24_out), .sel(Q[2]));
  FA fa_33 (.Co(fa_33_co), .S(fa_33_s), .Ci(1'b1), .A(A[6]), .B(not_8_out));
  Multiplexer #(.enable("false")) multiplexer_25 (.in0(A[6]), .in1(fa_33_s), .out(multiplexer_25_out), .sel(Q[6]));
  FA fa_34 (.Co(fa_34_co), .S(fa_34_s), .Ci(fa_40_co), .A(multiplexer_25_out), .B(not_7_out));
  Multiplexer #(.enable("false")) multiplexer_26 (
    .in0(multiplexer_25_out), .in1(fa_34_s), .out(multiplexer_26_out), .sel(Q[5]));
  FA fa_35 (.Co(fa_35_co), .S(fa_35_s), .Ci(fa_41_co), .A(multiplexer_26_out), .B(not_6_out));
  Multiplexer #(.enable("false")) multiplexer_27 (
    .in0(multiplexer_21_out), .in1(fa_32_s), .out(multiplexer_27_out), .sel(Q[4]));
  FA fa_36 (.Co(fa_36_co), .S(fa_36_s), .Ci(fa_42_co), .A(multiplexer_27_out), .B(not_4_out));
  Multiplexer #(.enable("false")) multiplexer_28 (
    .in0(multiplexer_27_out), .in1(fa_36_s), .out(multiplexer_28_out), .sel(Q[3]));
  FA fa_37 (.Co(fa_37_co), .S(fa_37_s), .Ci(fa_43_co), .A(multiplexer_28_out), .B(not_3_out));
  Multiplexer #(.enable("false")) multiplexer_29 (
    .in0(multiplexer_28_out), .in1(fa_37_s), .out(multiplexer_29_out), .sel(Q[2]));
  FA fa_38 (.Co(fa_38_co), .S(fa_38_s), .Ci(fa_44_co), .A(multiplexer_29_out), .B(not_2_out));
  Multiplexer #(.enable("false")) multiplexer_30 (
    .in0(multiplexer_29_out), .in1(fa_38_s), .out(multiplexer_30_out), .sel(Q[1]));
  FA fa_39 (.Co(Q[0]), .S(fa_39_s), .Ci(fa_45_co), .A(multiplexer_30_out), .B(not_1_out));
  Multiplexer #(.enable("false")) multiplexer_31 (.in0(multiplexer_30_out), .in1(fa_39_s), .out(R[7]), .sel(Q[0]));
  FA fa_40 (.Co(fa_40_co), .S(fa_40_s), .Ci(1'b1), .A(A[5]), .B(not_8_out));
  Multiplexer #(.enable("false")) multiplexer_32 (.in0(A[5]), .in1(fa_40_s), .out(multiplexer_32_out), .sel(Q[5]));
  FA fa_41 (.Co(fa_41_co), .S(fa_41_s), .Ci(fa_46_co), .A(multiplexer_32_out), .B(not_7_out));
  Multiplexer #(.enable("false")) multiplexer_33 (
    .in0(multiplexer_26_out), .in1(fa_35_s), .out(multiplexer_33_out), .sel(Q[4]));
  FA fa_42 (.Co(fa_42_co), .S(fa_42_s), .Ci(fa_47_co), .A(multiplexer_33_out), .B(not_5_out));
  Multiplexer #(.enable("false")) multiplexer_34 (
    .in0(multiplexer_33_out), .in1(fa_42_s), .out(multiplexer_34_out), .sel(Q[3]));
  FA fa_43 (.Co(fa_43_co), .S(fa_43_s), .Ci(fa_49_co), .A(multiplexer_34_out), .B(not_4_out));
  Multiplexer #(.enable("false")) multiplexer_35 (
    .in0(multiplexer_34_out), .in1(fa_43_s), .out(multiplexer_35_out), .sel(Q[2]));
  FA fa_44 (.Co(fa_44_co), .S(fa_44_s), .Ci(fa_50_co), .A(multiplexer_35_out), .B(not_3_out));
  Multiplexer #(.enable("false")) multiplexer_36 (
    .in0(multiplexer_35_out), .in1(fa_44_s), .out(multiplexer_36_out), .sel(Q[1]));
  FA fa_45 (.Co(fa_45_co), .S(fa_45_s), .Ci(fa_51_co), .A(multiplexer_36_out), .B(not_2_out));
  Multiplexer #(.enable("false")) multiplexer_37 (.in0(multiplexer_36_out), .in1(fa_45_s), .out(R[6]), .sel(Q[0]));
  FA fa_46 (.Co(fa_46_co), .S(fa_46_s), .Ci(1'b1), .A(A[4]), .B(not_8_out));
  Multiplexer #(.enable("false")) multiplexer_38 (
    .in0(multiplexer_32_out), .in1(fa_41_s), .out(multiplexer_38_out), .sel(Q[4]));
  Multiplexer #(.enable("false")) multiplexer_39 (.in0(A[4]), .in1(fa_46_s), .out(multiplexer_39_out), .sel(Q[4]));
  FA fa_47 (.Co(fa_47_co), .S(fa_47_s), .Ci(fa_48_co), .A(multiplexer_38_out), .B(not_6_out));
  FA fa_48 (.Co(fa_48_co), .S(fa_48_s), .Ci(fa_52_co), .A(multiplexer_39_out), .B(not_7_out));
  Multiplexer #(.enable("false")) multiplexer_40 (
    .in0(multiplexer_38_out), .in1(fa_47_s), .out(multiplexer_40_out), .sel(Q[3]));
  FA fa_49 (.Co(fa_49_co), .S(fa_49_s), .Ci(fa_53_co), .A(multiplexer_40_out), .B(not_5_out));
  Multiplexer #(.enable("false")) multiplexer_41 (
    .in0(multiplexer_40_out), .in1(fa_49_s), .out(multiplexer_41_out), .sel(Q[2]));
  FA fa_50 (.Co(fa_50_co), .S(fa_50_s), .Ci(fa_54_co), .A(multiplexer_41_out), .B(not_4_out));
  Multiplexer #(.enable("false")) multiplexer_42 (
    .in0(multiplexer_41_out), .in1(fa_50_s), .out(multiplexer_42_out), .sel(Q[1]));
  FA fa_51 (.Co(fa_51_co), .S(fa_51_s), .Ci(fa_55_co), .A(multiplexer_42_out), .B(not_3_out));
  Multiplexer #(.enable("false")) multiplexer_43 (.in0(multiplexer_42_out), .in1(fa_51_s), .out(R[5]), .sel(Q[0]));
  FA fa_52 (.Co(fa_52_co), .S(fa_52_s), .Ci(1'b1), .A(A[3]), .B(not_8_out));
  Multiplexer #(.enable("false")) multiplexer_44 (
    .in0(multiplexer_39_out), .in1(fa_48_s), .out(multiplexer_44_out), .sel(Q[3]));
  FA fa_53 (.Co(fa_53_co), .S(fa_53_s), .Ci(fa_56_co), .A(multiplexer_44_out), .B(not_6_out));
  Multiplexer #(.enable("false")) multiplexer_45 (
    .in0(multiplexer_44_out), .in1(fa_53_s), .out(multiplexer_45_out), .sel(Q[2]));
  FA fa_54 (.Co(fa_54_co), .S(fa_54_s), .Ci(fa_57_co), .A(multiplexer_45_out), .B(not_5_out));
  Multiplexer #(.enable("false")) multiplexer_46 (
    .in0(multiplexer_45_out), .in1(fa_54_s), .out(multiplexer_46_out), .sel(Q[1]));
  FA fa_55 (.Co(fa_55_co), .S(fa_55_s), .Ci(fa_58_co), .A(multiplexer_46_out), .B(not_4_out));
  Multiplexer #(.enable("false")) multiplexer_47 (.in0(multiplexer_46_out), .in1(fa_55_s), .out(R[4]), .sel(Q[0]));
  Multiplexer #(.enable("false")) multiplexer_48 (.in0(A[3]), .in1(fa_52_s), .out(multiplexer_48_out), .sel(Q[3]));
  FA fa_56 (.Co(fa_56_co), .S(fa_56_s), .Ci(fa_59_co), .A(multiplexer_48_out), .B(not_7_out));
  Multiplexer #(.enable("false")) multiplexer_49 (
    .in0(multiplexer_48_out), .in1(fa_56_s), .out(multiplexer_49_out), .sel(Q[2]));
  FA fa_57 (.Co(fa_57_co), .S(fa_57_s), .Ci(fa_60_co), .A(multiplexer_49_out), .B(not_6_out));
  Multiplexer #(.enable("false")) multiplexer_50 (
    .in0(multiplexer_49_out), .in1(fa_57_s), .out(multiplexer_50_out), .sel(Q[1]));
  FA fa_58 (.Co(fa_58_co), .S(fa_58_s), .Ci(fa_61_co), .A(multiplexer_50_out), .B(not_5_out));
  Multiplexer #(.enable("false")) multiplexer_51 (.in0(multiplexer_50_out), .in1(fa_58_s), .out(R[3]), .sel(Q[0]));
  FA fa_59 (.Co(fa_59_co), .S(fa_59_s), .Ci(1'b1), .A(A[2]), .B(not_8_out));
  Multiplexer #(.enable("false")) multiplexer_52 (.in0(A[2]), .in1(fa_59_s), .out(multiplexer_52_out), .sel(Q[2]));
  FA fa_60 (.Co(fa_60_co), .S(fa_60_s), .Ci(fa_62_co), .A(multiplexer_52_out), .B(not_7_out));
  Multiplexer #(.enable("false")) multiplexer_53 (
    .in0(multiplexer_52_out), .in1(fa_60_s), .out(multiplexer_53_out), .sel(Q[1]));
  FA fa_61 (.Co(fa_61_co), .S(fa_61_s), .Ci(fa_63_co), .A(multiplexer_53_out), .B(not_6_out));
  Multiplexer #(.enable("false")) multiplexer_54 (.in0(multiplexer_53_out), .in1(fa_61_s), .out(R[2]), .sel(Q[0]));
  FA fa_62 (.Co(fa_62_co), .S(fa_62_s), .Ci(1'b1), .A(A[1]), .B(not_8_out));
  Multiplexer #(.enable("false")) multiplexer_55 (.in0(A[1]), .in1(fa_62_s), .out(multiplexer_55_out), .sel(Q[1]));
  FA fa_63 (.Co(fa_63_co), .S(fa_63_s), .Ci(fa_64_co), .A(multiplexer_55_out), .B(not_7_out));
  Multiplexer #(.enable("false")) multiplexer_56 (.in0(multiplexer_55_out), .in1(fa_63_s), .out(R[1]), .sel(Q[0]));
  FA fa_64 (.Co(fa_64_co), .S(fa_64_s), .Ci(1'b1), .A(A[0]), .B(not_8_out));
  Multiplexer #(.enable("false")) multiplexer_57 (.in0(A[0]), .in1(fa_64_s), .out(R[0]), .sel(Q[0]));
endmodule

module FA (
  input  Ci,
  input  A,
  input  B,
  output Co,
  output S
);

  wire ha_1_c, ha_1_sum, ha_2_c;

  or or_1 (Co, ha_1_c, ha_2_c);
  HA ha_1 (.C(ha_1_c), .SUM(ha_1_sum), .A(A), .B(B));
  HA ha_2 (.C(ha_2_c), .SUM(S), .A(Ci), .B(ha_1_sum));
endmodule

module HA (
  input  A,
  input  B,
  output C,
  output SUM
);

  and and_1 (C, A, B);
  xor xor_1 (SUM, A, B);
endmodule
