// Logisim project 8bit_Multiplier.circ as structural Verilog: 3 circuits, main circuit main
module main (
  input  [7:0] A,
  input  [7:0] B,
  output [15:0] out_3,
  output out_4,
  output out_5,
  output out_6,
  output out_7,
  output out_8,
  output out_9,
  output out_10,
  output out_11,
  output out_12,
  output out_13,
  output out_14,
  output out_15,
  output out_16,
  output out_17,
  output out_18,
  output out_19
);

  wire a0b1, a0b2, a0b3, a0b4, a0b5, a0b6, a0b7, a1b0, a1b1, a1b2, a1b3, a1b4, a1b5, a1b6, a1b7, a2b0, a2b1,
       a2b2, a2b3, a2b4, a2b5, a2b6, a2b7, a3b0, a3b1, a3b2, a3b3, a3b4, a3b5, a3b6, a3b7, a4b0, a4b1, a4b2,
       a4b3, a4b4, a4b5, a4b6, a4b7, a5b0, a5b1, a5b2, a5b3, a5b4, a5b5, a5b6, a5b7, a6b0, a6b1, a6b2, a6b3,
       a6b4, a6b5, a6b6, a6b7, a7b0, a7b1, a7b2, a7b3, a7b4, a7b5, a7b6, a7b7, fa_2_co, fa_2_s, fa_3_co,
       fa_4_co, fa_4_s, fa_5_co, fa_5_s, fa_6_co, fa_7_co, fa_7_s, fa_8_co, fa_8_s, fa_9_co, fa_9_s,
       fa_10_co, fa_11_co, fa_11_s, fa_12_co, fa_12_s, fa_13_co, fa_13_s, fa_14_co, fa_14_s, fa_15_co,
       fa_16_co, fa_17_co, fa_17_s, fa_18_co, fa_18_s, fa_19_co, fa_19_s, fa_20_co, fa_20_s, fa_21_co,
       fa_21_s, fa_22_co, fa_22_s, fa_23_co, fa_24_co, fa_24_s, fa_25_co, fa_25_s, fa_26_co, fa_26_s,
       fa_27_co, fa_27_s, fa_28_co, fa_28_s, fa_29_co, fa_29_s, fa_30_co, fa_30_s, fa_31_co, fa_31_s,
       fa_32_co, fa_32_s, fa_33_co, fa_33_s, fa_34_co, fa_34_s, fa_35_co, fa_35_s, fa_36_co, fa_36_s,
       fa_37_co, fa_37_s, fa_38_co, fa_38_s, fa_39_co, fa_39_s, fa_40_co, fa_40_s, fa_41_co, fa_41_s,
       fa_42_co, fa_42_s, fa_43_co, fa_43_s, fa_44_co, fa_44_s, fa_45_co, fa_45_s, fa_46_co, fa_46_s,
       fa_47_co, fa_47_s, fa_48_co, fa_48_s, ha_1_c, ha_1_sum, ha_2_c, ha_3_c, ha_4_c, ha_5_c, ha_6_c,
       ha_7_c, ha_8_c;

  and and_1 (a7b7, A[7], B[7]);
  and and_2 (a6b7, A[6], B[7]);
  and and_3 (a5b7, A[5], B[7]);
  FA fa_1 (.Co(out_3[15]), .S(out_3[14]), .Ci(fa_3_co), .A(a7b7), .B(fa_2_co));
  and and_4 (a4b7, A[4], B[7]);
  and and_5 (a3b7, A[3], B[7]);
  FA fa_2 (.Co(fa_2_co), .S(fa_2_s), .Ci(fa_5_co), .A(a7b6), .B(fa_4_co));
  FA fa_3 (.Co(fa_3_co), .S(out_3[13]), .Ci(fa_6_co), .A(a6b7), .B(fa_2_s));
  and and_6 (a2b7, A[2], B[7]);
  FA fa_4 (.Co(fa_4_co), .S(fa_4_s), .Ci(fa_8_co), .A(a7b5), .B(fa_7_co));
  FA fa_5 (.Co(fa_5_co), .S(fa_5_s), .Ci(fa_9_co), .A(a6b6), .B(fa_4_s));
  FA fa_6 (.Co(fa_6_co), .S(out_3[12]), .Ci(fa_10_co), .A(a5b7), .B(fa_5_s));
  and and_7 (a1b7, A[1], B[7]);
  and and_8 (a0b7, A[0], B[7]);
  FA fa_7 (.Co(fa_7_co), .S(fa_7_s), .Ci(fa_12_co), .A(a7b4), .B(fa_11_co));
  FA fa_8 (.Co(fa_8_co), .S(fa_8_s), .Ci(fa_13_co), .A(a6b5), .B(fa_7_s));
  FA fa_9 (.Co(fa_9_co), .S(fa_9_s), .Ci(fa_14_co), .A(a5b6), .B(fa_8_s));
  FA fa_10 (.Co(fa_10_co), .S(out_3[11]), .Ci(fa_15_co), .A(a4b7), .B(fa_9_s));
  and and_9 (a7b6, A[7], B[6]);
  FA fa_11 (.Co(fa_11_co), .S(fa_11_s), .Ci(fa_18_co), .A(a7b3), .B(fa_17_co));
  FA fa_12 (.Co(fa_12_co), .S(fa_12_s), .Ci(fa_19_co), .A(a6b4), .B(fa_11_s));
  FA fa_13 (.Co(fa_13_co), .S(fa_13_s), .Ci(fa_20_co), .A(a5b5), .B(fa_12_s));
  FA fa_14 (.Co(fa_14_co), .S(fa_14_s), .Ci(fa_21_co), .A(a4b6), .B(fa_13_s));
  FA fa_15 (.Co(fa_15_co), .S(out_3[10]), .Ci(fa_16_co), .A(a3b7), .B(fa_14_s));
  FA fa_16 (.Co(fa_16_co), .S(out_3[9]), .Ci(fa_23_co), .A(a2b7), .B(fa_21_s));
  and and_10 (a6b6, A[6], B[6]);
  and and_11 (a5b6, A[5], B[6]);
  FA fa_17 (.Co(fa_17_co), .S(fa_17_s), .Ci(fa_24_co), .A(a7b2), .B(ha_1_c));
  FA fa_18 (.Co(fa_18_co), .S(fa_18_s), .Ci(fa_25_co), .A(a6b3), .B(fa_17_s));
  FA fa_19 (.Co(fa_19_co), .S(fa_19_s), .Ci(fa_26_co), .A(a5b4), .B(fa_18_s));
  FA fa_20 (.Co(fa_20_co), .S(fa_20_s), .Ci(fa_27_co), .A(a4b5), .B(fa_19_s));
  FA fa_21 (.Co(fa_21_co), .S(fa_21_s), .Ci(fa_22_co), .A(a3b6), .B(fa_20_s));
  FA fa_22 (.Co(fa_22_co), .S(fa_22_s), .Ci(fa_29_co), .A(a2b6), .B(fa_27_s));
  FA fa_23 (.Co(fa_23_co), .S(out_3[8]), .Ci(ha_2_c), .A(a1b7), .B(fa_22_s));
  and and_12 (a4b6, A[4], B[6]);
  HA ha_1 (.C(ha_1_c), .SUM(ha_1_sum), .A(a7b1), .B(fa_30_co));
  FA fa_24 (.Co(fa_24_co), .S(fa_24_s), .Ci(fa_31_co), .A(a6b2), .B(ha_1_sum));
  FA fa_25 (.Co(fa_25_co), .S(fa_25_s), .Ci(fa_32_co), .A(a5b3), .B(fa_24_s));
  FA fa_26 (.Co(fa_26_co), .S(fa_26_s), .Ci(fa_34_co), .A(a4b4), .B(fa_25_s));
  FA fa_27 (.Co(fa_27_co), .S(fa_27_s), .Ci(fa_28_co), .A(a3b5), .B(fa_26_s));
  FA fa_28 (.Co(fa_28_co), .S(fa_28_s), .Ci(fa_35_co), .A(a2b5), .B(fa_34_s));
  FA fa_29 (.Co(fa_29_co), .S(fa_29_s), .Ci(ha_3_c), .A(a1b6), .B(fa_28_s));
  HA ha_2 (.C(ha_2_c), .SUM(out_3[7]), .A(a0b7), .B(fa_29_s));
  and and_13 (a2b6, A[2], B[6]);
  and and_14 (a3b6, A[3], B[6]);
  FA fa_30 (.Co(fa_30_co), .S(fa_30_s), .Ci(fa_36_co), .A(a6b1), .B(a7b0));
  FA fa_31 (.Co(fa_31_co), .S(fa_31_s), .Ci(fa_37_co), .A(a5b2), .B(fa_30_s));
  FA fa_32 (.Co(fa_32_co), .S(fa_32_s), .Ci(fa_38_co), .A(a4b3), .B(fa_31_s));
  FA fa_33 (.Co(fa_33_co), .S(fa_33_s), .Ci(fa_40_co), .A(a2b4), .B(fa_38_s));
  FA fa_34 (.Co(fa_34_co), .S(fa_34_s), .Ci(fa_33_co), .A(a3b4), .B(fa_32_s));
  FA fa_35 (.Co(fa_35_co), .S(fa_35_s), .Ci(ha_4_c), .A(a1b5), .B(fa_33_s));
  HA ha_3 (.C(ha_3_c), .SUM(out_3[6]), .A(a0b6), .B(fa_35_s));
  and and_15 (a1b6, A[1], B[6]);
  FA fa_36 (.Co(fa_36_co), .S(fa_36_s), .Ci(fa_41_co), .A(a5b1), .B(a6b0));
  FA fa_37 (.Co(fa_37_co), .S(fa_37_s), .Ci(fa_42_co), .A(a4b2), .B(fa_36_s));
  FA fa_38 (.Co(fa_38_co), .S(fa_38_s), .Ci(fa_39_co), .A(a3b3), .B(fa_37_s));
  FA fa_39 (.Co(fa_39_co), .S(fa_39_s), .Ci(fa_44_co), .A(a2b3), .B(fa_42_s));
  FA fa_40 (.Co(fa_40_co), .S(fa_40_s), .Ci(ha_5_c), .A(a1b4), .B(fa_39_s));
  HA ha_4 (.C(ha_4_c), .SUM(out_3[5]), .A(a0b5), .B(fa_40_s));
  and and_16 (a0b6, A[0], B[6]);
  and and_17 (a7b5, A[7], B[5]);
  FA fa_41 (.Co(fa_41_co), .S(fa_41_s), .Ci(fa_45_co), .A(a4b1), .B(a5b0));
  FA fa_42 (.Co(fa_42_co), .S(fa_42_s), .Ci(fa_43_co), .A(a3b2), .B(fa_41_s));
  FA fa_43 (.Co(fa_43_co), .S(fa_43_s), .Ci(fa_47_co), .A(a2b2), .B(fa_45_s));
  FA fa_44 (.Co(fa_44_co), .S(fa_44_s), .Ci(ha_6_c), .A(a1b3), .B(fa_43_s));
  HA ha_5 (.C(ha_5_c), .SUM(out_3[4]), .A(a0b4), .B(fa_44_s));
  and and_18 (a6b5, A[6], B[5]);
  FA fa_45 (.Co(fa_45_co), .S(fa_45_s), .Ci(fa_46_co), .A(a3b1), .B(a4b0));
  FA fa_46 (.Co(fa_46_co), .S(fa_46_s), .Ci(fa_48_co), .A(a2b1), .B(a3b0));
  FA fa_47 (.Co(fa_47_co), .S(fa_47_s), .Ci(ha_7_c), .A(a1b2), .B(fa_46_s));
  HA ha_6 (.C(ha_6_c), .SUM(out_3[3]), .A(a0b3), .B(fa_47_s));
  and and_19 (a5b5, A[5], B[5]);
  and and_20 (a4b5, A[4], B[5]);
  FA fa_48 (.Co(fa_48_co), .S(fa_48_s), .Ci(ha_8_c), .A(a1b1), .B(a2b0));
  HA ha_7 (.C(ha_7_c), .SUM(out_3[2]), .A(a0b2), .B(fa_48_s));
  and and_21 (a3b5, A[3], B[5]);
  HA ha_8 (.C(ha_8_c), .SUM(out_3[1]), .A(a0b1), .B(a1b0));
  and and_22 (a2b5, A[2], B[5]);
  and and_23 (a1b5, A[1], B[5]);
  and and_24 (a0b5, A[0], B[5]);
  and and_25 (a7b4, A[7], B[4]);
  and and_26 (a6b4, A[6], B[4]);
  and and_27 (a5b4, A[5], B[4]);
  and and_28 (a4b4, A[4], B[4]);
  and and_29 (a3b4, A[3], B[4]);
  and and_30 (a2b4, A[2], B[4]);
  and and_31 (a1b4, A[1], B[4]);
  and and_32 (a0b4, A[0], B[4]);
  and and_33 (a7b3, A[7], B[3]);
  and and_34 (a6b3, A[6], B[3]);
  and and_35 (a5b3, A[5], B[3]);
  and and_36 (a4b3, A[4], B[3]);
  and and_37 (a3b3, A[3], B[3]);
  and and_38 (a2b3, A[2], B[3]);
  and and_39 (a1b3, A[1], B[3]);
  and and_40 (a0b3, A[0], B[3]);
  and and_41 (a7b2, A[7], B[2]);
  and and_42 (a6b2, A[6], B[2]);
  and and_43 (a5b2, A[5], B[2]);
  and and_44 (a4b2, A[4], B[2]);
  and and_45 (a3b2, A[3], B[2]);
  and and_46 (a2b2, A[2], B[2]);
  and and_47 (a1b2, A[1], B[2]);
  and and_48 (a0b2, A[0], B[2]);
  and and_49 (a7b1, A[7], B[1]);
  and and_50 (a6b1, A[6], B[1]);
  and and_51 (a5b1, A[5], B[1]);
  and and_52 (a4b1, A[4], B[1]);
  and and_53 (a3b1, A[3], B[1]);
  and and_54 (a2b1, A[2], B[1]);
  and and_55 (a1b1, A[1], B[1]);
  and and_56 (a0b1, A[0], B[1]);
  and and_57 (a7b0, A[7], B[0]);
  and and_58 (a6b0, A[6], B[0]);
  and and_59 (a5b0, A[5], B[0]);
  and and_60 (a4b0, A[4], B[0]);
  and and_61 (a3b0, A[3], B[0]);
  and and_62 (a2b0, A[2], B[0]);
  and and_63 (a1b0, A[1], B[0]);
  and and_64 (out_3[0], A[0], B[0]);

  assign out_4 = out_3[15];
  assign out_5 = out_3[14];
  assign out_6 = out_3[13];
  assign out_7 = out_3[12];
  assign out_8 = out_3[11];
  assign out_9 = out_3[10];
  assign out_10 = out_3[9];
  assign out_11 = out_3[8];
  assign out_12 = out_3[7];
  assign out_13 = out_3[6];
  assign out_14 = out_3[5];
  assign out_15 = out_3[4];
  assign out_16 = out_3[3];
  assign out_17 = out_3[2];
  assign out_18 = out_3[1];
  assign out_19 = out_3[0];

  // Other names for the same wires on the sheet: a0b0 = out_3[0]
endmodule

module HA (
  input  A,
  input  B,
  output C,
  output SUM
);

  and and_1 (C, A, B);
  xor xor_1 (SUM, A, B);
endmodule

module FA (
  input  Ci,
  input  A,
  input  B,
  output Co,
  output S
);

  wire ha_1_c, ha_1_sum, ha_2_c;

  or or_1 (Co, ha_1_c, ha_2_c);
  HA ha_1 (.C(ha_1_c), .SUM(ha_1_sum), .A(A), .B(B));
  HA ha_2 (.C(ha_2_c), .SUM(S), .A(Ci), .B(ha_1_sum));
endmodule
