// Logisim project FP32.circ as structural Verilog: 2 circuits, main circuit main
module main (
  input  [31:0] in_1,
  input  [31:0] in_2,
  output [31:0] out_3
);

  FP_add fp_add_1 (.in_1(in_1), .in_2(in_2), .out_3(out_3));
endmodule

module FP_add (
  input  [31:0] in_1,
  input  [31:0] in_2,
  output [31:0] out_3
);

  wire subtractor_1_bout;
  wire [0:0] adder_2_cout;
  wire [7:0] multiplexer_1_out, multiplexer_3_out, negator_1_out, subtractor_1_out;
  wire [23:0] adder_2_out, multiplexer_2_out, multiplexer_4_out, shifter_1_out;
  wire [23:23] shifter_2_out;

  xor xor_1 (out_3[31], in_1[31], in_2[31]);
  Subtractor subtractor_1 (
    .a(in_2[30:23]), .b(in_1[30:23]), .out(subtractor_1_out), .bout(subtractor_1_bout));  // open: bin
  Negator negator_1 (.in(subtractor_1_out), .out(negator_1_out));
  Multiplexer #(.enable("false"), .width(8)) multiplexer_1 (
    .in0(in_2[30:23]), .in1(in_1[30:23]), .out(multiplexer_1_out), .sel(subtractor_1_bout));
  Adder adder_1 (.a({8{1'b0}}), .b(multiplexer_1_out), .out(out_3[30:23]), .cin(adder_2_cout[0]));  // open: cout
  Multiplexer #(.enable("false"), .width(24)) multiplexer_2 (
    .in0({1'b1, in_1[22:0]}), .in1({1'b1, in_2[22:0]}), .out(multiplexer_2_out), .sel(subtractor_1_bout));
  Multiplexer #(.enable("false"), .width(8)) multiplexer_3 (
    .in0(subtractor_1_out), .in1(negator_1_out), .out(multiplexer_3_out), .sel(subtractor_1_bout));
  Multiplexer #(.enable("false"), .width(24)) multiplexer_4 (
    .in0({1'b1, in_2[22:0]}), .in1({1'b1, in_1[22:0]}), .out(multiplexer_4_out), .sel(subtractor_1_bout));
  Shifter #(.shift("lr"), .width(24)) shifter_1 (
    .in(multiplexer_2_out), .\dist (multiplexer_3_out[4:0]), .out(shifter_1_out));
  Adder #(.width(24)) adder_2 (
    .a(multiplexer_4_out), .b(shifter_1_out), .out(adder_2_out), .cout(adder_2_cout[0]));  // open: cin
  Shifter #(.shift("lr"), .width(24)) shifter_2 (
    .in(adder_2_out), .\dist ({4'b0000, adder_2_cout[0]}), .out({shifter_2_out[23], out_3[22:0]}));
endmodule
