// Logisim project Sequence_Detectors.circ as structural Verilog
module Mealy_011 (
  input  in_1,
  output out_2
);

  wire and_1_out, clock_1_out, d_ff_1_q, d_ff_2_q, not_1_out;

  Clock clock_1 (.out(clock_1_out));
  not not_1 (not_1_out, in_1);
  and and_1 (and_1_out, d_ff_1_q, in_1);
  D_Flip_Flop d_ff_1 (.clk(clock_1_out), .D(not_1_out), .Q(d_ff_1_q));  // open: Qn, preset, reset
  D_Flip_Flop d_ff_2 (.clk(clock_1_out), .D(and_1_out), .Q(d_ff_2_q));  // open: Qn, preset, reset
  and and_2 (out_2, in_1, d_ff_2_q);
endmodule

module Moore_011 (
  input  in_1,
  output out_2
);

  wire and_1_out, and_2_out, clock_1_out, d_ff_1_q, d_ff_1_qn, d_ff_2_q, not_1_out, or_1_out, xor_1_out;

  Clock clock_1 (.out(clock_1_out));
  not not_1 (not_1_out, in_1);
  or or_1 (or_1_out, not_1_out, and_1_out);
  and and_1 (and_1_out, d_ff_2_q, d_ff_1_qn);
  xor xor_1 (xor_1_out, d_ff_2_q, d_ff_1_q);
  and and_2 (and_2_out, xor_1_out, in_1);
  D_Flip_Flop d_ff_1 (.clk(clock_1_out), .D(or_1_out), .Q(d_ff_1_q), .Qn(d_ff_1_qn));  // open: preset, reset
  D_Flip_Flop d_ff_2 (.clk(clock_1_out), .D(and_2_out), .Q(d_ff_2_q));  // open: Qn, preset, reset
  and and_3 (out_2, d_ff_1_q, d_ff_2_q);
endmodule
