// Logisim project Shift_Registers_&_Counters.circ as structural Verilog: 14 circuits, main circuit main
module main (
);


  // Notes on the sheet:
  //   Asynchronous Counter
  //    1) +ve edge trigger	->	Q - clk	->	Down
  //   2) +ve edge trigger	->	Q' - clk	->	Up  
  //   1) -ve edge trigger	->	Q - clk	->	Up  
  //       2) -ve edge trigger	->	Q' - clk	->	Down
endmodule

module SISO (
  input  CLK,
  input  in_2,
  output out_3
);

  wire d_ff_1_q, d_ff_2_q, d_ff_3_q;

  D_Flip_Flop d_ff_1 (.clk(CLK), .D(in_2), .Q(d_ff_1_q));  // open: Qn, preset, reset
  D_Flip_Flop d_ff_2 (.clk(CLK), .D(d_ff_1_q), .Q(d_ff_2_q));  // open: Qn, preset, reset
  D_Flip_Flop d_ff_3 (.clk(CLK), .D(d_ff_2_q), .Q(d_ff_3_q));  // open: Qn, preset, reset
  D_Flip_Flop d_ff_4 (.clk(CLK), .D(d_ff_3_q), .Q(out_3));  // open: Qn, preset, reset
endmodule

module SIPO (
  input  CLK,
  input  in_2,
  output out_3,
  output out_4,
  output out_5,
  output out_6
);

  D_Flip_Flop d_ff_1 (.clk(CLK), .D(in_2), .Q(out_3));  // open: Qn, preset, reset
  D_Flip_Flop d_ff_2 (.clk(CLK), .D(out_3), .Q(out_4));  // open: Qn, preset, reset
  D_Flip_Flop d_ff_3 (.clk(CLK), .D(out_4), .Q(out_5));  // open: Qn, preset, reset
  D_Flip_Flop d_ff_4 (.clk(CLK), .D(out_5), .Q(out_6));  // open: Qn, preset, reset
endmodule

module PISO (
  input  in_1,
  input  in_2,
  input  in_3,
  input  in_4,
  input  CLK,
  input  LOAD__SHIFT_,
  output out_7
);

  wire d_ff_1_q, d_ff_2_q, d_ff_3_q, multiplexer_1_out, multiplexer_2_out, multiplexer_3_out,
       multiplexer_4_out, pull_resistor_1_node;

  Pull_Resistor pull_resistor_1 (.node(pull_resistor_1_node));
  Multiplexer #(.enable("false")) multiplexer_1 (
    .in0(pull_resistor_1_node), .in1(in_1), .out(multiplexer_1_out), .sel(LOAD__SHIFT_));
  D_Flip_Flop d_ff_1 (.clk(CLK), .D(multiplexer_1_out), .Q(d_ff_1_q));  // open: Qn, preset, reset
  Multiplexer #(.enable("false")) multiplexer_2 (
    .in0(d_ff_1_q), .in1(in_2), .out(multiplexer_2_out), .sel(LOAD__SHIFT_));
  D_Flip_Flop d_ff_2 (.clk(CLK), .D(multiplexer_2_out), .Q(d_ff_2_q));  // open: Qn, preset, reset
  Multiplexer #(.enable("false")) multiplexer_3 (
    .in0(d_ff_2_q), .in1(in_3), .out(multiplexer_3_out), .sel(LOAD__SHIFT_));
  D_Flip_Flop d_ff_3 (.clk(CLK), .D(multiplexer_3_out), .Q(d_ff_3_q));  // open: Qn, preset, reset
  Multiplexer #(.enable("false")) multiplexer_4 (
    .in0(d_ff_3_q), .in1(in_4), .out(multiplexer_4_out), .sel(LOAD__SHIFT_));
  D_Flip_Flop d_ff_4 (.clk(CLK), .D(multiplexer_4_out), .Q(out_7));  // open: Qn, preset, reset
endmodule

module PIPO (
  input  in_1,
  input  in_2,
  input  in_3,
  input  in_4,
  input  CLK,
  output out_6,
  output out_7,
  output out_8,
  output out_9
);

  D_Flip_Flop d_ff_1 (.clk(CLK), .D(in_1), .Q(out_6));  // open: Qn, preset, reset
  D_Flip_Flop d_ff_2 (.clk(CLK), .D(in_2), .Q(out_7));  // open: Qn, preset, reset
  D_Flip_Flop d_ff_3 (.clk(CLK), .D(in_3), .Q(out_8));  // open: Qn, preset, reset
  D_Flip_Flop d_ff_4 (.clk(CLK), .D(in_4), .Q(out_9));  // open: Qn, preset, reset
endmodule

module Bidirectional_sr (
  input  CLK,
  input  R_in,
  input  L_in,
  input  Right___Left,
  output L_out,
  output R_out
);

  wire d_ff_2_q, d_ff_3_q, multiplexer_1_out, multiplexer_2_out, multiplexer_3_out, multiplexer_4_out;

  Multiplexer #(.enable("false")) multiplexer_1 (
    .in0(R_in), .in1(d_ff_2_q), .out(multiplexer_1_out), .sel(Right___Left));
  D_Flip_Flop d_ff_1 (.clk(CLK), .D(multiplexer_1_out), .Q(L_out));  // open: Qn, preset, reset
  Multiplexer #(.enable("false")) multiplexer_2 (
    .in0(L_out), .in1(d_ff_3_q), .out(multiplexer_2_out), .sel(Right___Left));
  D_Flip_Flop d_ff_2 (.clk(CLK), .D(multiplexer_2_out), .Q(d_ff_2_q));  // open: Qn, preset, reset
  Multiplexer #(.enable("false")) multiplexer_3 (
    .in0(d_ff_2_q), .in1(R_out), .out(multiplexer_3_out), .sel(Right___Left));
  D_Flip_Flop d_ff_3 (.clk(CLK), .D(multiplexer_3_out), .Q(d_ff_3_q));  // open: Qn, preset, reset
  D_Flip_Flop d_ff_4 (.clk(CLK), .D(multiplexer_4_out), .Q(R_out));  // open: Qn, preset, reset
  Multiplexer #(.enable("false")) multiplexer_4 (
    .in0(d_ff_3_q), .in1(L_in), .out(multiplexer_4_out), .sel(Right___Left));
endmodule

module Async_Down_Counter (
  input  CLK,
  output out_2,
  output out_3,
  output out_4,
  output out_5
);

  T_Flip_Flop t_ff_1 (.clk(CLK), .T(1'b1), .Q(out_2));  // open: Qn, preset, reset
  T_Flip_Flop t_ff_2 (.clk(out_2), .T(1'b1), .Q(out_3));  // open: Qn, preset, reset
  T_Flip_Flop t_ff_3 (.clk(out_3), .T(1'b1), .Q(out_4));  // open: Qn, preset, reset
  T_Flip_Flop t_ff_4 (.clk(out_4), .T(1'b1), .Q(out_5));  // open: Qn, preset, reset
endmodule

module Async_Up_Counter (
  input  CLK,
  output out_2,
  output out_3,
  output out_4,
  output out_5
);

  wire t_ff_1_qn, t_ff_2_qn, t_ff_3_qn;

  T_Flip_Flop t_ff_1 (.clk(CLK), .T(1'b1), .Q(out_2), .Qn(t_ff_1_qn));  // open: preset, reset
  T_Flip_Flop t_ff_2 (.clk(t_ff_1_qn), .T(1'b1), .Q(out_3), .Qn(t_ff_2_qn));  // open: preset, reset
  T_Flip_Flop t_ff_3 (.clk(t_ff_2_qn), .T(1'b1), .Q(out_4), .Qn(t_ff_3_qn));  // open: preset, reset
  T_Flip_Flop t_ff_4 (.clk(t_ff_3_qn), .T(1'b1), .Q(out_5));  // open: Qn, preset, reset
endmodule

module Async_Up_Down_Counter (
  input  CLK,
  input  UP___DOWN,
  output out_3,
  output out_4,
  output out_5,
  output out_6
);

  wire multiplexer_1_out, multiplexer_2_out, multiplexer_3_out, t_ff_1_qn, t_ff_2_qn, t_ff_3_qn;

  T_Flip_Flop t_ff_1 (.clk(CLK), .T(1'b1), .Q(out_3), .Qn(t_ff_1_qn));  // open: preset, reset
  T_Flip_Flop t_ff_2 (.clk(multiplexer_1_out), .T(1'b1), .Q(out_4), .Qn(t_ff_2_qn));  // open: preset, reset
  Multiplexer #(.enable("false")) multiplexer_1 (
    .in0(out_3), .in1(t_ff_1_qn), .out(multiplexer_1_out), .sel(UP___DOWN));
  Multiplexer #(.enable("false")) multiplexer_2 (
    .in0(out_4), .in1(t_ff_2_qn), .out(multiplexer_2_out), .sel(UP___DOWN));
  T_Flip_Flop t_ff_3 (.clk(multiplexer_2_out), .T(1'b1), .Q(out_5), .Qn(t_ff_3_qn));  // open: preset, reset
  Multiplexer #(.enable("false")) multiplexer_3 (
    .in0(out_5), .in1(t_ff_3_qn), .out(multiplexer_3_out), .sel(UP___DOWN));
  T_Flip_Flop t_ff_4 (.clk(multiplexer_3_out), .T(1'b1), .Q(out_6));  // open: Qn, preset, reset
endmodule

module Sync_Up_Counter (
  input  CLK,
  output out_2,
  output out_3,
  output out_4,
  output out_5
);

  wire and_1_out, and_2_out;

  T_Flip_Flop t_ff_1 (.clk(CLK), .T(1'b1), .Q(out_2));  // open: Qn, preset, reset
  T_Flip_Flop t_ff_2 (.clk(CLK), .T(out_2), .Q(out_3));  // open: Qn, preset, reset
  and and_1 (and_1_out, out_3, out_2);
  T_Flip_Flop t_ff_3 (.clk(CLK), .T(and_1_out), .Q(out_4));  // open: Qn, preset, reset
  T_Flip_Flop t_ff_4 (.clk(CLK), .T(and_2_out), .Q(out_5));  // open: Qn, preset, reset
  and and_2 (and_2_out, out_4, and_1_out);
endmodule

module Sync_Down_Counter (
  input  CLK,
  output out_2,
  output out_3,
  output out_4,
  output out_5
);

  wire and_1_out, and_2_out, t_ff_1_qn, t_ff_2_qn, t_ff_3_qn;

  T_Flip_Flop t_ff_1 (.clk(CLK), .T(1'b1), .Q(out_2), .Qn(t_ff_1_qn));  // open: preset, reset
  T_Flip_Flop t_ff_2 (.clk(CLK), .T(t_ff_1_qn), .Q(out_3), .Qn(t_ff_2_qn));  // open: preset, reset
  and and_1 (and_1_out, t_ff_2_qn, t_ff_1_qn);
  T_Flip_Flop t_ff_3 (.clk(CLK), .T(and_1_out), .Q(out_4), .Qn(t_ff_3_qn));  // open: preset, reset
  T_Flip_Flop t_ff_4 (.clk(CLK), .T(and_2_out), .Q(out_5));  // open: Qn, preset, reset
  and and_2 (and_2_out, t_ff_3_qn, and_1_out);
endmodule

module _0_2_3_5_6_Counter (
  input  in_1,
  output out_2,
  output out_3,
  output out_4
);

  wire and_1_out, and_2_out, d_ff_1_qn, d_ff_2_qn, d_ff_3_qn, or_1_out;

  and and_1 (and_1_out, out_3, d_ff_3_qn);
  D_Flip_Flop d_ff_1 (.clk(in_1), .D(and_1_out), .Q(out_2), .Qn(d_ff_1_qn));  // open: preset, reset
  and and_2 (and_2_out, d_ff_1_qn, d_ff_3_qn);
  or or_1 (or_1_out, d_ff_2_qn, and_2_out);
  D_Flip_Flop d_ff_2 (.clk(in_1), .D(or_1_out), .Q(out_3), .Qn(d_ff_2_qn));  // open: preset, reset
  D_Flip_Flop d_ff_3 (.clk(in_1), .D(out_2), .Q(out_4), .Qn(d_ff_3_qn));  // open: preset, reset

  // Notes on the sheet:
  //   D0 = Q2'.Q1
  //   D1 = Q1' + Q2'.Q0'
  //   D2 = Q0
endmodule

module Ring_Counter (
  input  in_1,
  input  in_2
);

  wire [3:0] d_ff_1_q;

  D_Flip_Flop d_ff_1 (.clk(in_1), .D(d_ff_1_q[3]), .Q(d_ff_1_q[0]), .preset(in_2));  // open: Qn, reset
  D_Flip_Flop d_ff_2 (.clk(in_1), .D(d_ff_1_q[0]), .Q(d_ff_1_q[1]), .reset(in_2));  // open: Qn, preset
  D_Flip_Flop d_ff_3 (.clk(in_1), .D(d_ff_1_q[1]), .Q(d_ff_1_q[2]), .reset(in_2));  // open: Qn, preset
  D_Flip_Flop d_ff_4 (.clk(in_1), .D(d_ff_1_q[2]), .Q(d_ff_1_q[3]), .reset(in_2));  // open: Qn, preset
  Hex_Digit_Display hex_digit_display_1 (.value(d_ff_1_q));  // open: dp

  // Notes on the sheet:
  //   Ring Counter
  //   N bit -> mod N
endmodule

module Jhonson_Counter (
  input  in_1,
  input  in_2,
  input  in_3
);

  wire d_ff_4_qn;
  wire [3:0] d_ff_1_q;

  D_Flip_Flop d_ff_1 (.clk(in_1), .D(d_ff_4_qn), .Q(d_ff_1_q[0]), .preset(in_2), .reset(in_3));  // open: Qn
  D_Flip_Flop d_ff_2 (.clk(in_1), .D(d_ff_1_q[0]), .Q(d_ff_1_q[1]), .reset(in_3));  // open: Qn, preset
  D_Flip_Flop d_ff_3 (.clk(in_1), .D(d_ff_1_q[1]), .Q(d_ff_1_q[2]), .reset(in_3));  // open: Qn, preset
  D_Flip_Flop d_ff_4 (.clk(in_1), .D(d_ff_1_q[2]), .Q(d_ff_1_q[3]), .Qn(d_ff_4_qn), .reset(in_3));  // open: preset
  Hex_Digit_Display hex_digit_display_1 (.value(d_ff_1_q));  // open: dp

  // Notes on the sheet:
  //   Twisted Ring Counter (or) Jhonson Counter
  //   N bit -> mod 2N
endmodule
