// Logisim project booth_multiplier.circ as structural Verilog: 3 circuits, main circuit main
module main (
  input  in_1,
  input  in_2,
  input  in_3,
  input  in_4,
  input  in_5,
  input  in_6,
  input  in_7,
  input  in_8,
  input  in_9,
  output out_10,
  output out_11,
  output out_12,
  output out_13,
  output out_14,
  output out_15,
  output out_16,
  output out_17
);

  wire clock_1_out, comparator_1_eq, controlled_buffer_1_out, controlled_buffer_2_out, multiplexer_1_out,
       multiplexer_2_out, multiplexer_3_out, multiplexer_4_out, multiplexer_5_out, multiplexer_6_out,
       multiplexer_7_out, multiplexer_8_out;
  wire [2:0] counter_1_q;
  wire [3:0] adder_1_out, counter_2_q, disp_hex_1_hex1, disp_hex_1_hex2, disp_hex_1_hex3, disp_hex_1_hex4,
       rom_1_data, xor_4_out;

  Clock clock_1 (.out(clock_1_out));
  Counter #(.max('h1), .width(1)) counter_1 (
    .Q(counter_1_q[0]), .clk(clock_1_out), .clr(in_9));  // open: load, D, count, carry
  ROM #(.addrWidth(4), .dataWidth(4)) rom_1 (.addr({in_9, counter_1_q[2], out_17, counter_1_q[0]}), .data(rom_1_data));
  xor xor_1 (xor_4_out[3], in_1, out_17);
  xor xor_2 (xor_4_out[2], in_2, out_17);
  xor xor_3 (xor_4_out[1], in_3, out_17);
  xor xor_4 (xor_4_out[0], in_4, out_17);
  assign controlled_buffer_1_out = rom_1_data[0] ? clock_1_out : 1'bz;  // Controlled_Buffer controlled_buffer_1
  Adder #(.width(4)) adder_1 (
    .a(xor_4_out), .b({out_10, out_11, out_12, out_13}), .out(adder_1_out), .cin(out_17));  // open: cout
  Multiplexer #(.enable("false")) multiplexer_1 (
    .in0(out_10), .in1(adder_1_out[3]), .out(multiplexer_1_out), .sel(rom_1_data[1]));
  Multiplexer #(.enable("false")) multiplexer_2 (
    .in0(out_10), .in1(adder_1_out[2]), .out(multiplexer_2_out), .sel(rom_1_data[1]));
  D_Flip_Flop d_ff_1 (.clk(controlled_buffer_1_out), .D(multiplexer_1_out), .Q(out_10));  // open: Qn, preset, reset
  Counter #(.max('hf), .width(4)) counter_2 (.Q(counter_2_q), .clk(clock_1_out));  // open: load, D, count, carry, clr
  D_Flip_Flop d_ff_2 (.clk(controlled_buffer_1_out), .D(multiplexer_2_out), .Q(out_11));  // open: Qn, preset, reset
  Comparator #(.mode("unsigned"), .width(4)) comparator_1 (
    .a(counter_2_q), .b(4'b1001), .eq(comparator_1_eq));  // open: gt, lt
  Multiplexer #(.enable("false")) multiplexer_3 (
    .in0(out_11), .in1(adder_1_out[1]), .out(multiplexer_3_out), .sel(rom_1_data[1]));
  Multiplexer #(.enable("false")) multiplexer_4 (
    .in0(out_12), .in1(adder_1_out[0]), .out(multiplexer_4_out), .sel(rom_1_data[1]));
  D_Flip_Flop d_ff_3 (.clk(controlled_buffer_1_out), .D(multiplexer_3_out), .Q(out_12));  // open: Qn, preset, reset
  disp_hex disp_hex_1 (
    .IN({out_10, out_11, out_12, out_13, out_14, out_15, out_16, out_17}), .CLK(comparator_1_eq),
    .Sign(1'b1), .ENABLE(comparator_1_eq), .hex4(disp_hex_1_hex4), .hex3(disp_hex_1_hex3),
    .hex2(disp_hex_1_hex2), .hex1(disp_hex_1_hex1));
  D_Flip_Flop d_ff_4 (.clk(controlled_buffer_1_out), .D(multiplexer_4_out), .Q(out_13));  // open: Qn, preset, reset
  assign controlled_buffer_2_out = rom_1_data[3] ? clock_1_out : 1'bz;  // Controlled_Buffer controlled_buffer_2
  Hex_Digit_Display hex_digit_display_1 (.value(disp_hex_1_hex4));  // open: dp
  Hex_Digit_Display hex_digit_display_2 (.value(disp_hex_1_hex3));  // open: dp
  Multiplexer #(.enable("false")) multiplexer_5 (
    .in0(out_13), .in1(in_5), .out(multiplexer_5_out), .sel(rom_1_data[2]));
  Hex_Digit_Display hex_digit_display_3 (.value(disp_hex_1_hex2));  // open: dp
  Hex_Digit_Display hex_digit_display_4 (.value(disp_hex_1_hex1));  // open: dp
  Multiplexer #(.enable("false")) multiplexer_6 (
    .in0(out_14), .in1(in_6), .out(multiplexer_6_out), .sel(rom_1_data[2]));
  D_Flip_Flop d_ff_5 (.clk(controlled_buffer_2_out), .D(multiplexer_5_out), .Q(out_14));  // open: Qn, preset, reset
  D_Flip_Flop d_ff_6 (.clk(controlled_buffer_2_out), .D(multiplexer_6_out), .Q(out_15));  // open: Qn, preset, reset
  Multiplexer #(.enable("false")) multiplexer_7 (
    .in0(out_15), .in1(in_7), .out(multiplexer_7_out), .sel(rom_1_data[2]));
  Multiplexer #(.enable("false")) multiplexer_8 (
    .in0(out_16), .in1(in_8), .out(multiplexer_8_out), .sel(rom_1_data[2]));
  D_Flip_Flop d_ff_7 (.clk(controlled_buffer_2_out), .D(multiplexer_7_out), .Q(out_16));  // open: Qn, preset, reset
  D_Flip_Flop Q0 (.clk(controlled_buffer_2_out), .D(multiplexer_8_out), .Q(out_17));  // open: Qn, preset, reset
  D_Flip_Flop Q_1 (.clk(controlled_buffer_2_out), .D(out_17), .Q(counter_1_q[2]));  // open: Qn, preset, reset

  // Notes on the sheet:
  //   contents of rom_1 (hex, n*v repeats v):
  //   0 9 3 9 3 9 0 9 c
endmodule

module disp_hex (
  input  [7:0] IN,
  input  CLK,
  input  Sign,
  input  ENABLE,
  output [3:0] hex4,
  output [3:0] hex3,
  output [3:0] hex2,
  output [3:0] hex1
);

  wire comparator_1_gt, nand_1_out;
  wire [7:0] register_1_q;

  Register register_1 (.D(IN), .en(ENABLE), .Q(register_1_q), .clk(CLK));  // open: clr
  ROM #(.addrWidth(9), .dataWidth(12)) rom_1 (.addr({Sign, register_1_q}), .data({hex3, hex2, hex1}));
  Comparator #(.mode("unsigned")) comparator_1 (.a(register_1_q), .b(8'h7f), .gt(comparator_1_gt));  // open: eq, lt
  nand nand_1 (nand_1_out, Sign, comparator_1_gt);
  assign hex4 = nand_1_out ? 4'b0000 : 4'bz;  // Controlled_Buffer controlled_buffer_1

  // Notes on the sheet:
  //   contents of rom_1 (hex, n*v repeats v):
  //   0 1 2 3 4 5 6 7 8 9 10 11 12 13 14 15 16 17 18 19 20 21 22 23 24 25 26 27 28 29 30 31 32 33 34 35 36
  //   37 38 39 40 41 42 43 44 45 46 47 48 49 50 51 52 53 54 55 56 57 58 59 60 61 62 63 64 65 66 67 68 69
  //   70 71 72 73 74 75 76 77 78 79 80 81 82 83 84 85 86 87 88 89 90 91 92 93 94 95 96 97 98 99 100 101
  //   102 103 104 105 106 107 108 109 110 111 112 113 114 115 116 117 118 119 120 121 122 123 124 125 126
  //   127 128 129 130 131 132 133 134 135 136 137 138 139 140 141 142 143 144 145 146 147 148 149 150 151
  //   152 153 154 155 156 157 158 159 160 161 162 163 164 165 166 167 168 169 170 171 172 173 174 175 176
  //   177 178 179 180 181 182 183 184 185 186 187 188 189 190 191 192 193 194 195 196 197 198 199 200 201
  //   202 203 204 205 206 207 208 209 210 211 212 213 214 215 216 217 218 219 220 221 222 223 224 225 226
  //   227 228 229 230 231 232 233 234 235 236 237 238 239 240 241 242 243 244 245 246 247 248 249 250 251
  //   252 253 254 255 0 1 2 3 4 5 6 7 8 9 10 11 12 13 14 15 16 17 18 19 20 21 22 23 24 25 26 27 28 29 30
  //   31 32 33 34 35 36 37 38 39 40 41 42 43 44 45 46 47 48 49 50 51 52 53 54 55 56 57 58 59 60 61 62 63
  //   64 65 66 67 68 69 70 71 72 73 74 75 76 77 78 79 80 81 82 83 84 85 86 87 88 89 90 91 92 93 94 95 96
  //   97 98 99 100 101 102 103 104 105 106 107 108 109 110 111 112 113 114 115 116 117 118 119 120 121 122
  //   123 124 125 126 127 128 127 126 125 124 123 122 121 120 119 118 117 116 115 114 113 112 111 110 109
  //   108 107 106 105 104 103 102 101 100 99 98 97 96 95 94 93 92 91 90 89 88 87 86 85 84 83 82 81 80 79
  //   78 77 76 75 74 73 72 71 70 69 68 67 66 65 64 63 62 61 60 59 58 57 56 55 54 53 52 51 50 49 48 47 46
  //   45 44 43 42 41 40 39 38 37 36 35 34 33 32 31 30 29 28 27 26 25 24 23 22 21 20 19 18 17 16 15 14 13
  //   12 11 10 9 8 7 6 5 4 3 2 1
endmodule

module Control_Unit (
  input  L,
  input  Q1,
  input  Q0,
  input  s,
  output Y3,
  output Y2,
  output Y1,
  output Y0
);

  wire and_1_out, and_2_out, and_4_out, and_5_out, and_6_out, and_7_out, and_8_out;

  and and_1 (and_1_out, ~L, s);  // AND_Gate
  and and_2 (and_2_out, L, ~Q1, ~Q0, ~s);  // AND_Gate
  and and_3 (Y2, L, ~Q1, ~Q0, ~s);  // AND_Gate
  and and_4 (and_4_out, ~L, ~Q1, Q0, ~s);  // AND_Gate
  and and_5 (and_5_out, ~L, Q1, ~Q0, ~s);  // AND_Gate
  and and_6 (and_6_out, ~L, s);  // AND_Gate
  and and_7 (and_7_out, ~L, ~Q1, Q0);  // AND_Gate
  and and_8 (and_8_out, ~L, Q1, ~Q0);  // AND_Gate
  or or_1 (Y3, and_1_out, and_2_out);
  or or_2 (Y1, and_4_out, and_5_out);
  or or_3 (Y0, and_6_out, and_7_out, and_8_out);
endmodule
