// Logisim project freq_divider.circ as structural Verilog: 4 circuits, main circuit main
module main (
  output f_2,
  output f_3,
  output f_4,
  output f_5,
  output f_6
);

  wire clock_1_out, f_clk_3_1_f_clk_3;

  Clock clock_1 (.out(clock_1_out));
  T_Flip_Flop t_ff_1 (.clk(clock_1_out), .T(1'b1), .Q(f_2));  // open: Qn, preset, reset
  f_clk_3 f_clk_3_1 (.CLK(clock_1_out), .f_clk_3(f_clk_3_1_f_clk_3));
  T_Flip_Flop t_ff_2 (.clk(clock_1_out), .T(f_2), .Q(f_4));  // open: Qn, preset, reset
  f_clk_5 f_clk_5_1 (.CLK(clock_1_out), .f_clk_5(f_5));
  f_clk_6 f_clk_6_1 (.CLK(clock_1_out), .f_clk_6(f_6));
  not not_1 (f_3, f_clk_3_1_f_clk_3);
endmodule

module f_clk_3 (
  input  CLK,
  output f_clk_3
);

  wire and_1_out, d_ff_1_q, d_ff_1_qn, d_ff_2_q, d_ff_2_qn, d_ff_3_q;

  and and_1 (and_1_out, d_ff_2_qn, d_ff_1_qn);
  D_Flip_Flop d_ff_1 (.clk(CLK), .D(and_1_out), .Q(d_ff_1_q), .Qn(d_ff_1_qn));  // open: preset, reset
  D_Flip_Flop d_ff_2 (.clk(CLK), .D(d_ff_1_q), .Q(d_ff_2_q), .Qn(d_ff_2_qn));  // open: preset, reset
  D_Flip_Flop #(.trigger("falling")) d_ff_3 (.clk(CLK), .D(d_ff_2_q), .Q(d_ff_3_q));  // open: Qn, preset, reset
  or or_1 (f_clk_3, d_ff_2_q, d_ff_3_q);

  // Notes on the sheet:
  //   -ve edge
endmodule

module f_clk_5 (
  input  CLK,
  output f_clk_5
);

  wire and_1_out, and_2_out, d_ff_1_q, d_ff_1_qn, d_ff_2_q, d_ff_3_q, d_ff_3_qn, d_ff_4_q, xor_1_out;

  and and_1 (and_1_out, d_ff_3_qn, d_ff_1_qn);
  xor xor_1 (xor_1_out, d_ff_2_q, d_ff_1_q);
  and and_2 (and_2_out, d_ff_2_q, d_ff_1_q);
  D_Flip_Flop d_ff_1 (.clk(CLK), .D(and_1_out), .Q(d_ff_1_q), .Qn(d_ff_1_qn));  // open: preset, reset
  D_Flip_Flop d_ff_2 (.clk(CLK), .D(xor_1_out), .Q(d_ff_2_q));  // open: Qn, preset, reset
  D_Flip_Flop d_ff_3 (.clk(CLK), .D(and_2_out), .Q(d_ff_3_q), .Qn(d_ff_3_qn));  // open: preset, reset
  D_Flip_Flop #(.trigger("falling")) d_ff_4 (.clk(CLK), .D(d_ff_2_q), .Q(d_ff_4_q));  // open: Qn, preset, reset
  or or_1 (f_clk_5, d_ff_3_q, d_ff_4_q);

  // Notes on the sheet:
  //   -ve edge
endmodule

module f_clk_6 (
  input  CLK,
  output f_clk_6
);

  wire d_ff_1_q, d_ff_2_q, d_ff_3_qn;

  D_Flip_Flop d_ff_1 (.clk(CLK), .D(d_ff_3_qn), .Q(d_ff_1_q));  // open: Qn, preset, reset
  D_Flip_Flop d_ff_2 (.clk(CLK), .D(d_ff_1_q), .Q(d_ff_2_q));  // open: Qn, preset, reset
  D_Flip_Flop d_ff_3 (.clk(CLK), .D(d_ff_2_q), .Q(f_clk_6), .Qn(d_ff_3_qn));  // open: preset, reset
endmodule
