// Logisim project updown_counter.circ as structural Verilog: 1 circuit, main circuit main
module main (
  input  [3:0] in_1,
  input  [3:0] in_2,
  input  in_3,
  input  in_4
);

  wire clock_1_out, comparator_1_eq, comparator_2_eq, or_1_out, t_ff_1_q;
  wire [3:0] counter_1_q;
  wire [7:0] rom_1_data;

  or or_1 (or_1_out, comparator_2_eq, comparator_1_eq);
  T_Flip_Flop t_ff_1 (.clk(or_1_out), .T(in_3), .Q(t_ff_1_q));  // open: Qn, preset, reset
  Clock clock_1 (.out(clock_1_out));
  Counter #(.max('hf), .width(4)) counter_1 (
    .Q(counter_1_q), .up(t_ff_1_q), .clk(clock_1_out), .clr(in_4));  // open: load, D, count, carry
  Comparator #(.width(4)) comparator_1 (.a(in_1), .b(counter_1_q), .eq(comparator_1_eq));  // open: gt, lt
  Comparator #(.width(4)) comparator_2 (.a(in_2), .b(counter_1_q), .eq(comparator_2_eq));  // open: gt, lt
  ROM #(.addrWidth(4)) rom_1 (.addr(counter_1_q), .data(rom_1_data));
  _7_Segment_Display u_7_segment_display_1 (
    .g(rom_1_data[6]), .f(rom_1_data[5]), .a(rom_1_data[0]), .b(rom_1_data[1]), .e(rom_1_data[4]),
    .d(rom_1_data[3]), .c(rom_1_data[2]), .dp(rom_1_data[7]));

  // Notes on the sheet:
  //   contents of rom_1 (hex, n*v repeats v):
  //   3f 6 5b 4f 66 6d 7d 7 7f 6f 77 7c 39 5e 79 71
endmodule
