// Logisim project updown_counter_DFF.circ as structural Verilog: 1 circuit, main circuit main
// D2
module main (
  input  x,
  output Q0,
  output Q1,
  output Q2
);

  wire and_1_out, and_2_out, and_3_out, and_4_out, and_5_out, and_6_out, and_7_out, clock_1_out, D0_qn,
       D1_qn, D2_qn, not_1_out, or_1_out, or_2_out, xnor_1_out, xor_1_out;

  Clock clock_1 (.out(clock_1_out));
  not not_1 (not_1_out, x);
  D_Flip_Flop D0 (.clk(clock_1_out), .D(D0_qn), .Q(Q0), .Qn(D0_qn));  // open: preset, reset
  xnor xnor_1 (xnor_1_out, Q0, Q1);
  xor xor_1 (xor_1_out, Q0, Q1);
  D_Flip_Flop D1 (.clk(clock_1_out), .D(or_1_out), .Q(Q1), .Qn(D1_qn));  // open: preset, reset
  and and_1 (and_1_out, not_1_out, xnor_1_out);
  and and_2 (and_2_out, x, xor_1_out);
  or or_1 (or_1_out, and_1_out, and_2_out);
  D_Flip_Flop D2 (.clk(clock_1_out), .D(or_2_out), .Q(Q2), .Qn(D2_qn));  // open: preset, reset
  and and_3 (and_3_out, D2_qn, D1_qn, D0_qn, not_1_out);
  and and_4 (and_4_out, Q2, Q0, not_1_out);
  and and_5 (and_5_out, Q2, D1_qn, x);
  and and_6 (and_6_out, Q2, Q1, D0_qn);
  and and_7 (and_7_out, D2_qn, Q1, Q0, x);
  or or_2 (or_2_out, and_3_out, and_4_out, and_5_out, and_6_out, and_7_out);
endmodule
